// Logisim project drisc.circ as structural Verilog: 18 circuits, main circuit main
module main (
);

  wire Alu_Read, Call_Interrupt, Cl0ck, Connect_D_To_C, Data_IO_L_Read, Data_IO_Store, Decrement_Window,
       Enable_Interrupts, Increment_Window, io_controller_1_data_2bytes, io_controller_1_data_4bytes,
       io_controller_1_read_os_ram, io_controller_1_readkeyboard, io_controller_1_readram,
       io_controller_1_write_os_ram, io_controller_1_writeram, Is_Load_Store, Load_Immediate_High, not_1_out,
       or_1_out, PadRead, PadWrite, PC_Read_Current, PC_Read_Last, PC_Select_D_In, PC_Use_Offset,
       PC_Write_Next, Phase1, Phase1_q, Phase1n, Phase1s, Phase2, Phase2_q, Phase2i, Phase2n, Phase2s,
       Phase3, Phase3_q, Phase3i, Phase3n, Phase3s, por_1_out, por_2_out, por_3_out, por_4_out, por_5_out,
       por_6_out, por_7_out, por_8_out, por_9_out, por_10_out, por_11_out, por_12_out, por_13_out, PSW_Read,
       PSW_Set_Conditions, PSW_Write, Register_File_C_To_A, Register_File_Write, Relative, Shifter_C_Out,
       Shifter_L_In, Shifter_L_Out, Signed_Load, Use_19bit_Immediate,
       window_number_controller_1_window_overflow, Write_Window;
  wire [0:0] immediate_register_1_immediate_flag;
  wire [1:0] Data_Offset, Data_Size, Shift_Operation;
  wire [2:0] window_number_controller_1_window_number;
  wire [3:0] alu_1_overflow, Alu_Operation, processor_status_word_1_cnzv_out;
  wire [4:0] immediate_register_1_shift_amount;
  wire [6:0] keyboard_1_data;
  wire [7:0] data_input_output_1_pbus_out, data_input_output_1_pbus_out_2, data_input_output_1_pbus_out_3,
       data_input_output_1_pbus_out_4, demultiplexer_1_out0, io_controller_1_rom_address_out_8bit, ram_1_p8,
       shift_register_1_out, shift_register_1_q0, shift_register_1_q1, shift_register_1_q2,
       shift_register_1_q3, shift_register_1_q4, shift_register_1_q5, shift_register_1_q6,
       shift_register_1_q7, shift_register_1_q8, shift_register_1_q9, shift_register_1_q10,
       shift_register_1_q11, shift_register_1_q12, shift_register_1_q13, shift_register_1_q14,
       shift_register_1_q15, shift_register_1_q16, shift_register_1_q17, shift_register_1_q18,
       shift_register_1_q19, shift_register_1_q20, shift_register_1_q21, shift_register_1_q22,
       shift_register_1_q23, shift_register_1_q24, shift_register_1_q25, shift_register_1_q26,
       shift_register_1_q27, shift_register_1_q28, shift_register_1_q29, shift_register_1_q30,
       shift_register_1_q31, shift_register_1_q32, shift_register_1_q33, shift_register_1_q34,
       shift_register_1_q35, shift_register_1_q36, shift_register_1_q37, shift_register_1_q38,
       shift_register_1_q39, shift_register_1_q40, shift_register_1_q41, shift_register_1_q42,
       shift_register_1_q43, shift_register_1_q44, shift_register_1_q45, shift_register_1_q46,
       shift_register_1_q47, shift_register_1_q48, shift_register_1_q49, shift_register_1_q50,
       shift_register_1_q51, shift_register_1_q52, shift_register_1_q53, shift_register_1_q54,
       shift_register_1_q55, shift_register_1_q56, shift_register_1_q57, shift_register_1_q58,
       shift_register_1_q59, shift_register_1_q60, shift_register_1_q61, shift_register_1_q62,
       shift_register_2_out, shift_register_2_q0, shift_register_2_q1, shift_register_2_q2,
       shift_register_2_q3, shift_register_2_q4, shift_register_2_q5, shift_register_2_q6,
       shift_register_2_q7, shift_register_2_q8, shift_register_2_q9, shift_register_2_q10,
       shift_register_2_q11, shift_register_2_q12, shift_register_2_q13, shift_register_2_q14,
       shift_register_2_q15, shift_register_2_q16, shift_register_2_q17, shift_register_2_q18,
       shift_register_2_q19, shift_register_2_q20, shift_register_2_q21, shift_register_2_q22,
       shift_register_2_q23, shift_register_2_q24, shift_register_2_q25, shift_register_2_q26,
       shift_register_2_q27, shift_register_2_q28, shift_register_2_q29, shift_register_2_q30,
       shift_register_2_q31, shift_register_2_q32, shift_register_2_q33, shift_register_2_q34,
       shift_register_2_q35, shift_register_2_q36, shift_register_2_q37, shift_register_2_q38,
       shift_register_2_q39, shift_register_2_q40, shift_register_2_q41, shift_register_2_q42,
       shift_register_2_q43, shift_register_2_q44, shift_register_2_q45, shift_register_2_q46,
       shift_register_2_q47, shift_register_2_q48, shift_register_2_q49, shift_register_2_q50,
       shift_register_2_q51, shift_register_2_q52, shift_register_2_q53, shift_register_2_q54,
       shift_register_2_q55, shift_register_2_q56, shift_register_2_q57, shift_register_2_q58,
       shift_register_2_q59, shift_register_2_q60, shift_register_2_q61, shift_register_2_q62,
       shift_register_4_q0, shift_register_4_q1, shift_register_4_q2, shift_register_4_q3,
       shift_register_4_q4, shift_register_4_q5, shift_register_4_q6, shift_register_4_q7,
       shift_register_4_q8, shift_register_4_q9, shift_register_4_q10, shift_register_4_q11,
       shift_register_4_q12, shift_register_4_q13, shift_register_4_q14, shift_register_4_q15,
       shift_register_4_q16, shift_register_4_q17, shift_register_4_q18, shift_register_4_q19,
       shift_register_4_q20, shift_register_4_q21, shift_register_4_q22, shift_register_4_q23,
       shift_register_4_q24, shift_register_4_q25, shift_register_4_q26, shift_register_4_q27,
       shift_register_4_q28, shift_register_4_q29, shift_register_4_q30, shift_register_4_q31,
       shift_register_4_q32, shift_register_4_q33, shift_register_4_q34, shift_register_4_q35,
       shift_register_4_q36, shift_register_4_q37, shift_register_4_q38, shift_register_4_q39,
       shift_register_4_q40, shift_register_4_q41, shift_register_4_q42, shift_register_4_q43,
       shift_register_4_q44, shift_register_4_q45, shift_register_4_q46, shift_register_4_q47,
       shift_register_4_q48, shift_register_4_q49, shift_register_4_q50, shift_register_4_q51,
       shift_register_4_q52, shift_register_4_q53, shift_register_4_q54, shift_register_4_q55,
       shift_register_4_q56, shift_register_4_q57, shift_register_4_q58, shift_register_4_q59,
       shift_register_4_q60, shift_register_4_q61, shift_register_4_q62, shift_register_5_p5,
       shift_register_5_p6, shift_register_5_p7;
  wire [7:7] keyboard_1_avail;
  wire [9:0] processor_status_word_1_d, shift_register_3_q0, shift_register_3_q1, shift_register_3_q2,
       shift_register_3_q3, shift_register_3_q4, shift_register_3_q5, shift_register_3_q6,
       shift_register_3_q7, shift_register_3_q8, shift_register_3_q9, shift_register_3_q10,
       shift_register_3_q11, shift_register_3_q12, shift_register_3_q13, shift_register_3_q14,
       shift_register_3_q15, shift_register_3_q16, shift_register_3_q17, shift_register_3_q18,
       shift_register_3_q19, shift_register_3_q20, shift_register_3_q21, shift_register_3_q22,
       shift_register_3_q23, shift_register_3_q24, shift_register_3_q25, shift_register_3_q26,
       shift_register_3_q27, shift_register_3_q28, shift_register_3_q29, shift_register_3_q30,
       shift_register_3_q31, shift_register_3_q32, shift_register_3_q33, shift_register_3_q34,
       shift_register_3_q35, shift_register_3_q36, shift_register_3_q37, shift_register_3_q38,
       shift_register_3_q39, shift_register_3_q40, shift_register_3_q41, shift_register_3_q42,
       shift_register_3_q43, shift_register_3_q44, shift_register_3_q45, shift_register_3_q46,
       shift_register_3_q47, shift_register_3_q48, shift_register_3_q49, shift_register_3_q50,
       shift_register_3_q51, shift_register_3_q52, shift_register_3_q53, shift_register_3_q54,
       shift_register_3_q55, shift_register_3_q56, shift_register_3_q57, shift_register_3_q58,
       shift_register_3_q59, shift_register_3_q60, shift_register_3_q61, shift_register_3_q62;
  wire [23:0] io_controller_1_address_out_24bit;
  wire [31:0] alu_1_result, buffer_1_out, immediate_register_1_immediate_13bit,
       immediate_register_1_immediate_19bit, io_controller_1_addressdebug, program_counter_1_c_bus_out,
       program_counter_1_p_bus_out, program_counter_1_program_counter_out, register_file_1_a_bus_out,
       register_file_1_b_bus_out, shifter_circuit_1_c_bus_out, window_number_controller_1_lbus_out;

  Demultiplexer #(.select(3)) demultiplexer_1 (
    .out0(demultiplexer_1_out0[0]), .out1(demultiplexer_1_out0[1]), .out2(demultiplexer_1_out0[2]),
    .out3(demultiplexer_1_out0[3]), .out4(demultiplexer_1_out0[4]), .out5(demultiplexer_1_out0[5]),
    .out6(demultiplexer_1_out0[6]), .out7(demultiplexer_1_out0[7]), .in(1'b1),
    .sel(window_number_controller_1_window_number));
  Shift_Register #(.length(64), .width(8)) shift_register_1 (
    .in(demultiplexer_1_out0), .clk(Write_Window), .out(shift_register_1_out), .clr(por_1_out),
    .q0(shift_register_1_q0), .q1(shift_register_1_q1), .q2(shift_register_1_q2), .q3(shift_register_1_q3),
    .q4(shift_register_1_q4), .q5(shift_register_1_q5), .q6(shift_register_1_q6), .q7(shift_register_1_q7),
    .q8(shift_register_1_q8), .q9(shift_register_1_q9), .q10(shift_register_1_q10),
    .q11(shift_register_1_q11), .q12(shift_register_1_q12), .q13(shift_register_1_q13),
    .q14(shift_register_1_q14), .q15(shift_register_1_q15), .q16(shift_register_1_q16),
    .q17(shift_register_1_q17), .q18(shift_register_1_q18), .q19(shift_register_1_q19),
    .q20(shift_register_1_q20), .q21(shift_register_1_q21), .q22(shift_register_1_q22),
    .q23(shift_register_1_q23), .q24(shift_register_1_q24), .q25(shift_register_1_q25),
    .q26(shift_register_1_q26), .q27(shift_register_1_q27), .q28(shift_register_1_q28),
    .q29(shift_register_1_q29), .q30(shift_register_1_q30), .q31(shift_register_1_q31),
    .q32(shift_register_1_q32), .q33(shift_register_1_q33), .q34(shift_register_1_q34),
    .q35(shift_register_1_q35), .q36(shift_register_1_q36), .q37(shift_register_1_q37),
    .q38(shift_register_1_q38), .q39(shift_register_1_q39), .q40(shift_register_1_q40),
    .q41(shift_register_1_q41), .q42(shift_register_1_q42), .q43(shift_register_1_q43),
    .q44(shift_register_1_q44), .q45(shift_register_1_q45), .q46(shift_register_1_q46),
    .q47(shift_register_1_q47), .q48(shift_register_1_q48), .q49(shift_register_1_q49),
    .q50(shift_register_1_q50), .q51(shift_register_1_q51), .q52(shift_register_1_q52),
    .q53(shift_register_1_q53), .q54(shift_register_1_q54), .q55(shift_register_1_q55),
    .q56(shift_register_1_q56), .q57(shift_register_1_q57), .q58(shift_register_1_q58),
    .q59(shift_register_1_q59), .q60(shift_register_1_q60), .q61(shift_register_1_q61),
    .q62(shift_register_1_q62));  // open: shift, load, d0, d1, d2, d3, d4, d5, d6, d7, d8, d9, d10, d11, d12, d13, d14, d15, d16, d17, d18, d19, d20, d21, d22, d23, d24, d25, d26, d27, d28, d29, d30, d31, d32, d33, d34, d35, d36, d37, d38, d39, d40, d41, d42, d43, d44, d45, d46, d47, d48, d49, d50, d51, d52, d53, d54, d55, d56, d57, d58, d59, d60, d61, d62, d63, q63
  POR #(.porsize(2)) por_1 (.out(por_1_out));
  DotMatrix #(.matrixcols(63), .matrixrows(8)) dotmatrix_1 (
    .col0(shift_register_1_q0), .col1(shift_register_1_q1), .col2(shift_register_1_q2),
    .col3(shift_register_1_q3), .col4(shift_register_1_q4), .col5(shift_register_1_q5),
    .col6(shift_register_1_q6), .col7(shift_register_1_q7), .col8(shift_register_1_q8),
    .col9(shift_register_1_q9), .col10(shift_register_1_q10), .col11(shift_register_1_q11),
    .col12(shift_register_1_q12), .col13(shift_register_1_q13), .col14(shift_register_1_q14),
    .col15(shift_register_1_q15), .col16(shift_register_1_q16), .col17(shift_register_1_q17),
    .col18(shift_register_1_q18), .col19(shift_register_1_q19), .col20(shift_register_1_q20),
    .col21(shift_register_1_q21), .col22(shift_register_1_q22), .col23(shift_register_1_q23),
    .col24(shift_register_1_q24), .col25(shift_register_1_q25), .col26(shift_register_1_q26),
    .col27(shift_register_1_q27), .col28(shift_register_1_q28), .col29(shift_register_1_q29),
    .col30(shift_register_1_q30), .col31(shift_register_1_q31), .col32(shift_register_1_q32),
    .col33(shift_register_1_q33), .col34(shift_register_1_q34), .col35(shift_register_1_q35),
    .col36(shift_register_1_q36), .col37(shift_register_1_q37), .col38(shift_register_1_q38),
    .col39(shift_register_1_q39), .col40(shift_register_1_q40), .col41(shift_register_1_q41),
    .col42(shift_register_1_q42), .col43(shift_register_1_q43), .col44(shift_register_1_q44),
    .col45(shift_register_1_q45), .col46(shift_register_1_q46), .col47(shift_register_1_q47),
    .col48(shift_register_1_q48), .col49(shift_register_1_q49), .col50(shift_register_1_q50),
    .col51(shift_register_1_q51), .col52(shift_register_1_q52), .col53(shift_register_1_q53),
    .col54(shift_register_1_q54), .col55(shift_register_1_q55), .col56(shift_register_1_q56),
    .col57(shift_register_1_q57), .col58(shift_register_1_q58), .col59(shift_register_1_q59),
    .col60(shift_register_1_q60), .col61(shift_register_1_q61), .col62(shift_register_1_q62));
  POR #(.porsize(2)) por_2 (.out(por_2_out));
  // Probe on window_number_controller_1_window_number
  Register_File register_file_1 (
    .C_Bus_In(buffer_1_out),
    .P_Bus_in({data_input_output_1_pbus_out_4, data_input_output_1_pbus_out_3, data_input_output_1_pbus_out_2, data_input_output_1_pbus_out}),
    .Write_Interrupt_Register(Phase2i), .Reset(por_3_out), .Clock(Cl0ck), .Write_Next_Addresses(Phase2n),
    .Write_Current_Adresses(Phase1n), .Write_C_Address_To_A(Register_File_C_To_A),
    .Window_Number(window_number_controller_1_window_number), .Read(Phase1), .Write(Register_File_Write),
    .A_Bus_Out(register_file_1_a_bus_out), .B_Bus_Out(register_file_1_b_bus_out));
  POR #(.porsize(2)) por_3 (.out(por_3_out));
  Window_Number_Controller window_number_controller_1 (
    .Increment_Window(Increment_Window), .LBus_In(window_number_controller_1_lbus_out), .Clock(Cl0ck),
    .Write(Write_Window), .Reset(por_2_out), .Read(Phase3n), .Decrement_Window(Decrement_Window),
    .Window_Overflow(window_number_controller_1_window_overflow),
    .LBus_Out(window_number_controller_1_lbus_out), .Window_Number(window_number_controller_1_window_number));
  // Probe on register_file_1_a_bus_out
  // Probe on register_file_1_b_bus_out
  // Probe on buffer_1_out
  // Probe on {data_input_output_1_pbus_out_4, data_input_output_1_pbus_out_3, data_input_output_1_pbus_out_2, data_input_output_1_pbus_out}
  // Probe on window_number_controller_1_lbus_out
  Shift_Register #(.length(64), .width(8)) shift_register_2 (
    .in(shift_register_1_out), .clk(Write_Window), .out(shift_register_2_out), .clr(por_4_out),
    .q0(shift_register_2_q0), .q1(shift_register_2_q1), .q2(shift_register_2_q2), .q3(shift_register_2_q3),
    .q4(shift_register_2_q4), .q5(shift_register_2_q5), .q6(shift_register_2_q6), .q7(shift_register_2_q7),
    .q8(shift_register_2_q8), .q9(shift_register_2_q9), .q10(shift_register_2_q10),
    .q11(shift_register_2_q11), .q12(shift_register_2_q12), .q13(shift_register_2_q13),
    .q14(shift_register_2_q14), .q15(shift_register_2_q15), .q16(shift_register_2_q16),
    .q17(shift_register_2_q17), .q18(shift_register_2_q18), .q19(shift_register_2_q19),
    .q20(shift_register_2_q20), .q21(shift_register_2_q21), .q22(shift_register_2_q22),
    .q23(shift_register_2_q23), .q24(shift_register_2_q24), .q25(shift_register_2_q25),
    .q26(shift_register_2_q26), .q27(shift_register_2_q27), .q28(shift_register_2_q28),
    .q29(shift_register_2_q29), .q30(shift_register_2_q30), .q31(shift_register_2_q31),
    .q32(shift_register_2_q32), .q33(shift_register_2_q33), .q34(shift_register_2_q34),
    .q35(shift_register_2_q35), .q36(shift_register_2_q36), .q37(shift_register_2_q37),
    .q38(shift_register_2_q38), .q39(shift_register_2_q39), .q40(shift_register_2_q40),
    .q41(shift_register_2_q41), .q42(shift_register_2_q42), .q43(shift_register_2_q43),
    .q44(shift_register_2_q44), .q45(shift_register_2_q45), .q46(shift_register_2_q46),
    .q47(shift_register_2_q47), .q48(shift_register_2_q48), .q49(shift_register_2_q49),
    .q50(shift_register_2_q50), .q51(shift_register_2_q51), .q52(shift_register_2_q52),
    .q53(shift_register_2_q53), .q54(shift_register_2_q54), .q55(shift_register_2_q55),
    .q56(shift_register_2_q56), .q57(shift_register_2_q57), .q58(shift_register_2_q58),
    .q59(shift_register_2_q59), .q60(shift_register_2_q60), .q61(shift_register_2_q61),
    .q62(shift_register_2_q62));  // open: shift, load, d0, d1, d2, d3, d4, d5, d6, d7, d8, d9, d10, d11, d12, d13, d14, d15, d16, d17, d18, d19, d20, d21, d22, d23, d24, d25, d26, d27, d28, d29, d30, d31, d32, d33, d34, d35, d36, d37, d38, d39, d40, d41, d42, d43, d44, d45, d46, d47, d48, d49, d50, d51, d52, d53, d54, d55, d56, d57, d58, d59, d60, d61, d62, d63, q63
  POR #(.porsize(2)) por_4 (.out(por_4_out));
  DotMatrix #(.matrixcols(63), .matrixrows(8)) dotmatrix_2 (
    .col0(shift_register_2_q0), .col1(shift_register_2_q1), .col2(shift_register_2_q2),
    .col3(shift_register_2_q3), .col4(shift_register_2_q4), .col5(shift_register_2_q5),
    .col6(shift_register_2_q6), .col7(shift_register_2_q7), .col8(shift_register_2_q8),
    .col9(shift_register_2_q9), .col10(shift_register_2_q10), .col11(shift_register_2_q11),
    .col12(shift_register_2_q12), .col13(shift_register_2_q13), .col14(shift_register_2_q14),
    .col15(shift_register_2_q15), .col16(shift_register_2_q16), .col17(shift_register_2_q17),
    .col18(shift_register_2_q18), .col19(shift_register_2_q19), .col20(shift_register_2_q20),
    .col21(shift_register_2_q21), .col22(shift_register_2_q22), .col23(shift_register_2_q23),
    .col24(shift_register_2_q24), .col25(shift_register_2_q25), .col26(shift_register_2_q26),
    .col27(shift_register_2_q27), .col28(shift_register_2_q28), .col29(shift_register_2_q29),
    .col30(shift_register_2_q30), .col31(shift_register_2_q31), .col32(shift_register_2_q32),
    .col33(shift_register_2_q33), .col34(shift_register_2_q34), .col35(shift_register_2_q35),
    .col36(shift_register_2_q36), .col37(shift_register_2_q37), .col38(shift_register_2_q38),
    .col39(shift_register_2_q39), .col40(shift_register_2_q40), .col41(shift_register_2_q41),
    .col42(shift_register_2_q42), .col43(shift_register_2_q43), .col44(shift_register_2_q44),
    .col45(shift_register_2_q45), .col46(shift_register_2_q46), .col47(shift_register_2_q47),
    .col48(shift_register_2_q48), .col49(shift_register_2_q49), .col50(shift_register_2_q50),
    .col51(shift_register_2_q51), .col52(shift_register_2_q52), .col53(shift_register_2_q53),
    .col54(shift_register_2_q54), .col55(shift_register_2_q55), .col56(shift_register_2_q56),
    .col57(shift_register_2_q57), .col58(shift_register_2_q58), .col59(shift_register_2_q59),
    .col60(shift_register_2_q60), .col61(shift_register_2_q61), .col62(shift_register_2_q62));
  Data_Input_Output data_input_output_1 (
    .Data_Offset(Data_Offset), .Data_Size(Data_Size), .Read_To_L(Data_IO_L_Read),
    .LBus_In(window_number_controller_1_lbus_out), .Write_From_L(Data_IO_Store),
    .PBus_In({data_input_output_1_pbus_out_4, data_input_output_1_pbus_out_3, data_input_output_1_pbus_out_2, data_input_output_1_pbus_out}),
    .Read_To_P(Data_IO_Store), .Write_From_P(Phase1s), .Clock(Cl0ck), .Signed_Data(Signed_Load),
    .Lbus_Out(window_number_controller_1_lbus_out),
    .PBus_Out({data_input_output_1_pbus_out_4, data_input_output_1_pbus_out_3, data_input_output_1_pbus_out_2, data_input_output_1_pbus_out}));
  Shifter_Circuit shifter_circuit_1 (
    .Enable_C_Out(Shifter_C_Out), .Byte_Control_In(Data_Offset), .Clock(Cl0ck),
    .Select_Byte_Control(Is_Load_Store), .Select_Immediate(immediate_register_1_immediate_flag[0]),
    .B_Bus_In(register_file_1_b_bus_out), .Immediate_In(immediate_register_1_shift_amount),
    .A_Bus_In(register_file_1_a_bus_out), .Write(Phase1), .Enable_L_Out(Shifter_L_Out),
    .LBus_In(window_number_controller_1_lbus_out), .Enable_L_In(Shifter_L_In),
    .Operation_Select(Shift_Operation), .Calculate(Phase2), .C_Bus_Out(shifter_circuit_1_c_bus_out),
    .LBus_Out(window_number_controller_1_lbus_out));
  assign buffer_1_out = shifter_circuit_1_c_bus_out;  // Buffer buffer_1, 32 bits wide
  or or_1 (or_1_out, PSW_Set_Conditions, PSW_Write);
  POR #(.PorHighDuration(1), .porsize(2)) por_5 (.out(por_5_out));
  // Probe on shifter_circuit_1_c_bus_out
  Shift_Register #(.length(64), .width(10)) shift_register_3 (
    .shift(or_1_out), .in(processor_status_word_1_d), .clk(Cl0ck), .q0(shift_register_3_q0),
    .q1(shift_register_3_q1), .q2(shift_register_3_q2), .q3(shift_register_3_q3), .q4(shift_register_3_q4),
    .q5(shift_register_3_q5), .q6(shift_register_3_q6), .q7(shift_register_3_q7), .q8(shift_register_3_q8),
    .q9(shift_register_3_q9), .q10(shift_register_3_q10), .q11(shift_register_3_q11),
    .q12(shift_register_3_q12), .q13(shift_register_3_q13), .q14(shift_register_3_q14),
    .q15(shift_register_3_q15), .q16(shift_register_3_q16), .q17(shift_register_3_q17),
    .q18(shift_register_3_q18), .q19(shift_register_3_q19), .q20(shift_register_3_q20),
    .q21(shift_register_3_q21), .q22(shift_register_3_q22), .q23(shift_register_3_q23),
    .q24(shift_register_3_q24), .q25(shift_register_3_q25), .q26(shift_register_3_q26),
    .q27(shift_register_3_q27), .q28(shift_register_3_q28), .q29(shift_register_3_q29),
    .q30(shift_register_3_q30), .q31(shift_register_3_q31), .q32(shift_register_3_q32),
    .q33(shift_register_3_q33), .q34(shift_register_3_q34), .q35(shift_register_3_q35),
    .q36(shift_register_3_q36), .q37(shift_register_3_q37), .q38(shift_register_3_q38),
    .q39(shift_register_3_q39), .q40(shift_register_3_q40), .q41(shift_register_3_q41),
    .q42(shift_register_3_q42), .q43(shift_register_3_q43), .q44(shift_register_3_q44),
    .q45(shift_register_3_q45), .q46(shift_register_3_q46), .q47(shift_register_3_q47),
    .q48(shift_register_3_q48), .q49(shift_register_3_q49), .q50(shift_register_3_q50),
    .q51(shift_register_3_q51), .q52(shift_register_3_q52), .q53(shift_register_3_q53),
    .q54(shift_register_3_q54), .q55(shift_register_3_q55), .q56(shift_register_3_q56),
    .q57(shift_register_3_q57), .q58(shift_register_3_q58), .q59(shift_register_3_q59),
    .q60(shift_register_3_q60), .q61(shift_register_3_q61), .q62(shift_register_3_q62));  // open: out, load, clr, d0, d1, d2, d3, d4, d5, d6, d7, d8, d9, d10, d11, d12, d13, d14, d15, d16, d17, d18, d19, d20, d21, d22, d23, d24, d25, d26, d27, d28, d29, d30, d31, d32, d33, d34, d35, d36, d37, d38, d39, d40, d41, d42, d43, d44, d45, d46, d47, d48, d49, d50, d51, d52, d53, d54, d55, d56, d57, d58, d59, d60, d61, d62, d63, q63
  DotMatrix #(.matrixcols(63), .matrixrows(10)) dotmatrix_3 (
    .col0(shift_register_3_q0), .col1(shift_register_3_q1), .col2(shift_register_3_q2),
    .col3(shift_register_3_q3), .col4(shift_register_3_q4), .col5(shift_register_3_q5),
    .col6(shift_register_3_q6), .col7(shift_register_3_q7), .col8(shift_register_3_q8),
    .col9(shift_register_3_q9), .col10(shift_register_3_q10), .col11(shift_register_3_q11),
    .col12(shift_register_3_q12), .col13(shift_register_3_q13), .col14(shift_register_3_q14),
    .col15(shift_register_3_q15), .col16(shift_register_3_q16), .col17(shift_register_3_q17),
    .col18(shift_register_3_q18), .col19(shift_register_3_q19), .col20(shift_register_3_q20),
    .col21(shift_register_3_q21), .col22(shift_register_3_q22), .col23(shift_register_3_q23),
    .col24(shift_register_3_q24), .col25(shift_register_3_q25), .col26(shift_register_3_q26),
    .col27(shift_register_3_q27), .col28(shift_register_3_q28), .col29(shift_register_3_q29),
    .col30(shift_register_3_q30), .col31(shift_register_3_q31), .col32(shift_register_3_q32),
    .col33(shift_register_3_q33), .col34(shift_register_3_q34), .col35(shift_register_3_q35),
    .col36(shift_register_3_q36), .col37(shift_register_3_q37), .col38(shift_register_3_q38),
    .col39(shift_register_3_q39), .col40(shift_register_3_q40), .col41(shift_register_3_q41),
    .col42(shift_register_3_q42), .col43(shift_register_3_q43), .col44(shift_register_3_q44),
    .col45(shift_register_3_q45), .col46(shift_register_3_q46), .col47(shift_register_3_q47),
    .col48(shift_register_3_q48), .col49(shift_register_3_q49), .col50(shift_register_3_q50),
    .col51(shift_register_3_q51), .col52(shift_register_3_q52), .col53(shift_register_3_q53),
    .col54(shift_register_3_q54), .col55(shift_register_3_q55), .col56(shift_register_3_q56),
    .col57(shift_register_3_q57), .col58(shift_register_3_q58), .col59(shift_register_3_q59),
    .col60(shift_register_3_q60), .col61(shift_register_3_q61), .col62(shift_register_3_q62));
  Immediate_Register immediate_register_1 (
    .LoadHigh(Load_Immediate_High),
    .Pbus_In({data_input_output_1_pbus_out_4, data_input_output_1_pbus_out_3, data_input_output_1_pbus_out_2, data_input_output_1_pbus_out}),
    .Write_Enable(Phase2n), .Clock(Cl0ck), .Reset(por_5_out),
    .Immediate_13bit(immediate_register_1_immediate_13bit),
    .Immediate_19bit(immediate_register_1_immediate_19bit), .Shift_Amount(immediate_register_1_shift_amount),
    .Immediate_Flag(immediate_register_1_immediate_flag[0]));
  POR #(.PorHighDuration(1), .porsize(2)) por_6 (.out(por_6_out));
  // Probe on immediate_register_1_immediate_19bit
  Processor_Status_Word processor_status_word_1 (
    .Read(PSW_Read), .LBus_in(window_number_controller_1_lbus_out), .CNZV_in(alu_1_overflow),
    .Set_Condition_Code(PSW_Set_Conditions), .Write(PSW_Write), .Clock(Cl0ck), .Reset(por_6_out),
    .d(processor_status_word_1_d), .Lbus_out(window_number_controller_1_lbus_out),
    .CNZV_out(processor_status_word_1_cnzv_out));
  Shift_Register #(.length(64), .width(8)) shift_register_4 (
    .in(shift_register_2_out), .clk(Write_Window), .clr(por_7_out), .q0(shift_register_4_q0),
    .q1(shift_register_4_q1), .q2(shift_register_4_q2), .q3(shift_register_4_q3), .q4(shift_register_4_q4),
    .q5(shift_register_4_q5), .q6(shift_register_4_q6), .q7(shift_register_4_q7), .q8(shift_register_4_q8),
    .q9(shift_register_4_q9), .q10(shift_register_4_q10), .q11(shift_register_4_q11),
    .q12(shift_register_4_q12), .q13(shift_register_4_q13), .q14(shift_register_4_q14),
    .q15(shift_register_4_q15), .q16(shift_register_4_q16), .q17(shift_register_4_q17),
    .q18(shift_register_4_q18), .q19(shift_register_4_q19), .q20(shift_register_4_q20),
    .q21(shift_register_4_q21), .q22(shift_register_4_q22), .q23(shift_register_4_q23),
    .q24(shift_register_4_q24), .q25(shift_register_4_q25), .q26(shift_register_4_q26),
    .q27(shift_register_4_q27), .q28(shift_register_4_q28), .q29(shift_register_4_q29),
    .q30(shift_register_4_q30), .q31(shift_register_4_q31), .q32(shift_register_4_q32),
    .q33(shift_register_4_q33), .q34(shift_register_4_q34), .q35(shift_register_4_q35),
    .q36(shift_register_4_q36), .q37(shift_register_4_q37), .q38(shift_register_4_q38),
    .q39(shift_register_4_q39), .q40(shift_register_4_q40), .q41(shift_register_4_q41),
    .q42(shift_register_4_q42), .q43(shift_register_4_q43), .q44(shift_register_4_q44),
    .q45(shift_register_4_q45), .q46(shift_register_4_q46), .q47(shift_register_4_q47),
    .q48(shift_register_4_q48), .q49(shift_register_4_q49), .q50(shift_register_4_q50),
    .q51(shift_register_4_q51), .q52(shift_register_4_q52), .q53(shift_register_4_q53),
    .q54(shift_register_4_q54), .q55(shift_register_4_q55), .q56(shift_register_4_q56),
    .q57(shift_register_4_q57), .q58(shift_register_4_q58), .q59(shift_register_4_q59),
    .q60(shift_register_4_q60), .q61(shift_register_4_q61), .q62(shift_register_4_q62));  // open: shift, out, load, d0, d1, d2, d3, d4, d5, d6, d7, d8, d9, d10, d11, d12, d13, d14, d15, d16, d17, d18, d19, d20, d21, d22, d23, d24, d25, d26, d27, d28, d29, d30, d31, d32, d33, d34, d35, d36, d37, d38, d39, d40, d41, d42, d43, d44, d45, d46, d47, d48, d49, d50, d51, d52, d53, d54, d55, d56, d57, d58, d59, d60, d61, d62, d63, q63
  POR #(.porsize(2)) por_7 (.out(por_7_out));
  DotMatrix #(.matrixcols(63), .matrixrows(8)) dotmatrix_4 (
    .col0(shift_register_4_q0), .col1(shift_register_4_q1), .col2(shift_register_4_q2),
    .col3(shift_register_4_q3), .col4(shift_register_4_q4), .col5(shift_register_4_q5),
    .col6(shift_register_4_q6), .col7(shift_register_4_q7), .col8(shift_register_4_q8),
    .col9(shift_register_4_q9), .col10(shift_register_4_q10), .col11(shift_register_4_q11),
    .col12(shift_register_4_q12), .col13(shift_register_4_q13), .col14(shift_register_4_q14),
    .col15(shift_register_4_q15), .col16(shift_register_4_q16), .col17(shift_register_4_q17),
    .col18(shift_register_4_q18), .col19(shift_register_4_q19), .col20(shift_register_4_q20),
    .col21(shift_register_4_q21), .col22(shift_register_4_q22), .col23(shift_register_4_q23),
    .col24(shift_register_4_q24), .col25(shift_register_4_q25), .col26(shift_register_4_q26),
    .col27(shift_register_4_q27), .col28(shift_register_4_q28), .col29(shift_register_4_q29),
    .col30(shift_register_4_q30), .col31(shift_register_4_q31), .col32(shift_register_4_q32),
    .col33(shift_register_4_q33), .col34(shift_register_4_q34), .col35(shift_register_4_q35),
    .col36(shift_register_4_q36), .col37(shift_register_4_q37), .col38(shift_register_4_q38),
    .col39(shift_register_4_q39), .col40(shift_register_4_q40), .col41(shift_register_4_q41),
    .col42(shift_register_4_q42), .col43(shift_register_4_q43), .col44(shift_register_4_q44),
    .col45(shift_register_4_q45), .col46(shift_register_4_q46), .col47(shift_register_4_q47),
    .col48(shift_register_4_q48), .col49(shift_register_4_q49), .col50(shift_register_4_q50),
    .col51(shift_register_4_q51), .col52(shift_register_4_q52), .col53(shift_register_4_q53),
    .col54(shift_register_4_q54), .col55(shift_register_4_q55), .col56(shift_register_4_q56),
    .col57(shift_register_4_q57), .col58(shift_register_4_q58), .col59(shift_register_4_q59),
    .col60(shift_register_4_q60), .col61(shift_register_4_q61), .col62(shift_register_4_q62));
  POR #(.PorHighDuration(1), .porsize(2)) por_8 (.out(por_8_out));
  Clock clock_1 (.out(Cl0ck));
  not not_1 (not_1_out, Cl0ck);
  // Probe on alu_1_overflow
  D_Flip_Flop u_Phase1 (.clk(not_1_out), .D(Phase3_q), .Q(Phase1_q), .preset(por_9_out));  // open: Qn, reset
  POR #(.PorHighDuration(1), .porsize(2)) por_9 (.out(por_9_out));
  POR #(.PorHighDuration(1), .porsize(2)) por_10 (.out(por_10_out));
  D_Flip_Flop u_Phase2 (.clk(not_1_out), .D(Phase1_q), .Q(Phase2_q), .reset(por_9_out));  // open: Qn, preset
  ALU alu_1 (
    .Calculate(Phase2), .Read(Alu_Read), .Clock(Cl0ck), .Source2(register_file_1_b_bus_out),
    .Immediate_13bit(immediate_register_1_immediate_13bit),
    .Immediate_19bit(immediate_register_1_immediate_19bit), .Input_Select1({1'b0, Relative}),
    .Source1(register_file_1_a_bus_out), .Program_Counter_In(program_counter_1_program_counter_out),
    .Input_Select2({Use_19bit_Immediate, immediate_register_1_immediate_flag[0]}), .Write(Phase1),
    .Reset(por_8_out), .Carry_In(processor_status_word_1_cnzv_out[3]), .Operation(Alu_Operation),
    .Negative(alu_1_overflow[2]), .Overflow(alu_1_overflow[0]), .Carry_Out(alu_1_overflow[3]),
    .Zero(alu_1_overflow[1]), .Result(alu_1_result));
  // Probe on alu_1_result
  assign buffer_1_out = Connect_D_To_C ? alu_1_result : 32'bz;  // Controlled_Buffer controlled_buffer_1
  D_Flip_Flop u_Phase3 (.clk(not_1_out), .D(Phase2_q), .Q(Phase3_q), .reset(por_9_out));  // open: Qn, preset
  Clock_Circuit clock_circuit_1 (
    .Phase3_in(Phase3_q), .Load_Store_Instruction(Is_Load_Store),
    .Window_Overflow(window_number_controller_1_window_overflow),
    .Return_Interrupt_Instruction(Enable_Interrupts), .Interrupt(Call_Interrupt), .Reset(por_10_out),
    .Phase1_In(Phase1_q), .Phase2_In(Phase2_q), .Phase3(Phase3), .Phase3i(Phase3i), .Phase3n(Phase3n),
    .Phase3s(Phase3s), .Phase1(Phase1), .Phase1n(Phase1n), .Phase1s(Phase1s), .Phase2(Phase2),
    .Phase2i(Phase2i), .Phase2n(Phase2n), .Phase2s(Phase2s));
  POR #(.PorHighDuration(1), .porsize(2)) por_11 (.out(por_11_out));
  // Probe on {Phase3i, Phase2i, Phase3s, Phase2s, Phase1s, Phase3n, Phase2n, Phase1n}
  Operation_Controller operation_controller_1 (
    .P_Bus_In({data_input_output_1_pbus_out_4, data_input_output_1_pbus_out_3, data_input_output_1_pbus_out_2, data_input_output_1_pbus_out}),
    .Clock(Cl0ck), .CNZV_In(processor_status_word_1_cnzv_out), .Reset(por_11_out), .Phase1n(Phase1n),
    .Phase2n(Phase2n), .Phase3n(Phase3n), .Phase1s(Phase1s), .Phase2s(Phase2s), .Phase3s(Phase3s),
    .Phase2i(Phase2i), .Phase3i(Phase3i), .Signed_Load(Signed_Load), .ALU_Operation(Alu_Operation),
    .Shift_Operation(Shift_Operation), .Data_Size(Data_Size), .Set_Condition_Code(PSW_Set_Conditions),
    .Register_File_C_Address_To_A(Register_File_C_To_A), .Register_File_Write(Register_File_Write),
    .Window_Number_Decrement(Decrement_Window), .Window_Number_Increment(Increment_Window),
    .Enable_Interrupt_Bit(Enable_Interrupts), .Interrupt_Call(Call_Interrupt), .Status_Word_Write(PSW_Write),
    .Status_Word_Read(PSW_Read), .Window_Number_Write(Write_Window), .Data_IO_Store(Data_IO_Store),
    .Data_IO_L_Read(Data_IO_L_Read), .PC_Use_Offset(PC_Use_Offset), .Alu_Read(Alu_Read),
    .PC_Write_Next(PC_Write_Next), .PC_Read_Current(PC_Read_Current), .PC_Read_Last(PC_Read_Last),
    .PC_Select_D_In(PC_Select_D_In), .Shifter_Read_C(Shifter_C_Out), .Load_Store(Is_Load_Store),
    .PAD_Write(PadWrite), .PAD_Read(PadRead), .Shifter_Write_L(Shifter_L_In), .Shifter_Read_L(Shifter_L_Out),
    .Select_High_Immediate(Load_Immediate_High), .ALU_Use_19bit_Immediate(Use_19bit_Immediate),
    .Relative(Relative), .Connect_D_C_Bus(Connect_D_To_C));
  POR #(.porsize(2)) por_12 (.out(por_12_out));
  Program_Counter program_counter_1 (
    .Enable_Current_Out(PC_Read_Current), .Write_Last(Phase1n), .Enable_Last_Out(PC_Read_Last),
    .D_Bus_In(alu_1_result), .Enable_D_In(PC_Select_D_In), .Reset(por_12_out), .Clock(Cl0ck),
    .Load_Interrupt_Vector(Phase3i), .Write_Next(PC_Write_Next), .Use_Offset(PC_Use_Offset),
    .D_Bus_To_P(Phase3s), .Next_P_Out(Phase1n), .Write_Current(Phase2n), .Byte_Offset(Data_Offset),
    .P_Bus_Out(program_counter_1_p_bus_out), .Program_Counter_Out(program_counter_1_program_counter_out),
    .C_Bus_Out(program_counter_1_c_bus_out));
  // Probe on program_counter_1_c_bus_out
  assign buffer_1_out = program_counter_1_c_bus_out;  // Buffer buffer_2, 32 bits wide
  assign {data_input_output_1_pbus_out_4, data_input_output_1_pbus_out_3, data_input_output_1_pbus_out_2, data_input_output_1_pbus_out} = program_counter_1_p_bus_out;  // Buffer buffer_3, 32 bits wide
  // Probe on program_counter_1_p_bus_out
  Keyboard keyboard_1 (.clk(Cl0ck), .re(1'b1), .avail(keyboard_1_avail[7]), .data(keyboard_1_data));  // open: clr
  // Probe on io_controller_1_addressdebug
  POR #(.PorHighDuration(1), .porsize(2)) por_13 (.out(por_13_out));
  IO_Controller io_controller_1 (
    .Phase1n(Phase1n), .Phase3s(Phase3s), .Phase3i(Phase3i),
    .Address_In({data_input_output_1_pbus_out_4, data_input_output_1_pbus_out_3, data_input_output_1_pbus_out_2, data_input_output_1_pbus_out}),
    .Clock(Cl0ck), .Reset(por_13_out), .Write(PadWrite), .Data_Size(Data_Size), .Read(PadRead),
    .AddressDebug(io_controller_1_addressdebug), .ReadRam(io_controller_1_readram),
    .ReadKeyboard(io_controller_1_readkeyboard), .Read_OS_Ram(io_controller_1_read_os_ram),
    .WriteRam(io_controller_1_writeram), .Write_OS_Ram(io_controller_1_write_os_ram),
    .Data_2Bytes(io_controller_1_data_2bytes), .Data_4Bytes(io_controller_1_data_4bytes),
    .Address_Out_24Bit(io_controller_1_address_out_24bit),
    .Rom_Address_Out_8Bit(io_controller_1_rom_address_out_8bit));
  // Shift_Register #(.length(4), .width(8)) shift_register_5: pin names not known; wires that end beside it: Phase3s, keyboard_1_avail[7], Cl0ck, {keyboard_1_avail[7], keyboard_1_data}, shift_register_5_p5, shift_register_5_p6, shift_register_5_p7
  // Digital_Oscilloscope digital_oscilloscope_1: pin names not known; wires that end beside it: Cl0ck, io_controller_1_write_os_ram, io_controller_1_read_os_ram
  // RAM #(.addrWidth(24), .databus("bidir"), .enables("line"), .line("quad"), .misaligned("true"), .trigger("high"), .\type ("nonvolatile")) ram_1: pin names not known; wires that end beside it: io_controller_1_address_out_24bit, io_controller_1_writeram, io_controller_1_readram, 1'b1, io_controller_1_data_2bytes, io_controller_1_data_4bytes, Cl0ck, ram_1_p8
  ROM #(.dataWidth(32)) rom_1 (
    .addr(io_controller_1_rom_address_out_8bit),
    .data({data_input_output_1_pbus_out_4, data_input_output_1_pbus_out_3, data_input_output_1_pbus_out_2, data_input_output_1_pbus_out}));
  // RAM #(.addrWidth(24), .clearpin("true"), .databus("bidir"), .enables("line"), .line("quad"), .misaligned("true"), .trigger("high"), .\type ("nonvolatile")) ram_2: pin names not known; wires that end beside it: io_controller_1_address_out_24bit, io_controller_1_write_os_ram, io_controller_1_read_os_ram, 1'b1, io_controller_1_data_2bytes, io_controller_1_data_4bytes, Cl0ck
  Button R ();  // open: out
  assign {data_input_output_1_pbus_out_4, data_input_output_1_pbus_out_3, data_input_output_1_pbus_out_2, data_input_output_1_pbus_out} = io_controller_1_readkeyboard ? {ram_1_p8, shift_register_5_p7, shift_register_5_p6, shift_register_5_p5} : 32'bz;  // Controlled_Buffer controlled_buffer_2
  // Digital_Oscilloscope digital_oscilloscope_2: pin names not known; wires that end beside it: Cl0ck, io_controller_1_writeram, io_controller_1_readram

  // Notes on the sheet:
  //   Program Counter(Dline)
  //   contents of rom_1 (hex, n*v repeats v):
  //   d0c00000 25b80000 b1b5a001 21b5a01f e1ae0000 51a56000 519e6000 e1940000 a19cc012 150da0ac b1000000
  //   71d52004 71dd2008 71e5200c 71f52010 71ed2014 71fd2018 b1dd2000 19502004 7182e01c 718ae020 7192e024
  //   719ae028 71a2e02c 71aae030 71b2e034 71bae038 71c2e03c 71cae040 b152a034 c100000a b1a52040 71a56000
  //   b1a5e010 81a52070 b1ade080 81ad6380 81bdfc0f 91bdc014 91bdc015 3505c000 147e4000 c87e0000 b1fbe000
  //   b1f3a000 b1eb6000 b1e32000 b1dae000 b1d2a000 c1000010 b1fe6000 b1f62000 b1ede000 b1e56000 b1dd2000
  //   11802000 b1cbe000 b1c3a000 b1bb6000 b1ab2000 b1a2e000 c1000010 51cee040 51c6e03c 51bee038 51b6e034
  //   51aee030 51a6e02c 519ee028 5196e024 518ee020 5186e01c 517ee018 5176e014 516ee010 5166e00c 515ee008
  //   5156e004 11b02000 b17fe000 b177a000 b16f6000 b1672000 b15ee000 b156a000 a1a52040 71a56000 a1bde010
  //   b1fe6000 b1f62000 b1ede000 11c80000 35034000 147bc000 c87b8000
  //   Interrupt Routines ROM
  //   OS RAM
endmodule

module Clock_Circuit (
  input  Interrupt,
  input  Reset,
  input  Phase1_In,
  input  Phase2_In,
  input  Phase3_in,
  input  Load_Store_Instruction,
  input  Window_Overflow,
  input  Return_Interrupt_Instruction,
  output Phase2n,
  output Phase1,
  output Phase1s,
  output Phase2,
  output Phase3,
  output Phase3n,
  output Phase2s,
  output Phase1n,
  output Phase2i,
  output Phase3i,
  output Phase3s
);

  wire and_1_out, and_2_out, and_8_out, and_12_out, Interrupt_Enable_q, Interruption_q, not_1_out, not_2_out,
       not_3_out, or_1_out, or_2_out, or_3_out, SecondaryA_q, SecondaryB_q;

  and and_1 (and_1_out, Return_Interrupt_Instruction, Phase3n);
  or or_1 (or_1_out, Interrupt, Window_Overflow);
  Register #(.trigger("high"), .width(1)) Interrupt_Enable (
    .D(and_1_out), .en(and_1_out), .clk(1'b1), .Q(Interrupt_Enable_q), .clr(or_2_out));
  or or_2 (or_2_out, Phase2i, Reset);
  and and_2 (and_2_out, or_1_out, Interrupt_Enable_q);
  or or_3 (or_3_out, Reset, and_2_out);
  and and_3 (Phase1n, not_2_out, Phase1_In);
  and and_4 (Phase1s, SecondaryA_q, Phase1_In);
  Register #(.trigger("high"), .width(1)) Interruption (
    .D(or_3_out), .en(Phase1_In), .clk(Phase1_In), .Q(Interruption_q), .clr(Reset));
  not not_1 (not_1_out, Interruption_q);
  and and_5 (Phase2i, Interruption_q, Phase2_In);
  and and_6 (Phase2n, not_3_out, not_1_out, Phase2_In);
  and and_7 (Phase2s, SecondaryB_q, not_1_out, Phase2_In);
  Register #(.trigger("high"), .width(1)) SecondaryA (
    .D(and_8_out), .en(Phase2_In), .clk(Phase2_In), .Q(SecondaryA_q), .clr(Reset));
  and and_8 (and_8_out, Load_Store_Instruction, not_3_out);
  not not_2 (not_2_out, SecondaryA_q);
  and and_9 (Phase3i, Interruption_q, Phase3_in);
  and and_10 (Phase3n, not_2_out, not_1_out, Phase3_in);
  and and_11 (Phase3s, SecondaryA_q, not_1_out, Phase3_in);
  Register #(.trigger("high"), .width(1)) SecondaryB (
    .D(and_12_out), .en(Phase3_in), .clk(Phase3_in), .Q(SecondaryB_q), .clr(Reset));
  and and_12 (and_12_out, not_1_out, SecondaryA_q);
  not not_3 (not_3_out, SecondaryB_q);

  assign Phase1 = Phase1_In;
  assign Phase2 = Phase2_In;
  assign Phase3 = Phase3_in;
endmodule

module ALU (
  input  [3:0] Operation,
  input  Write,
  input  Carry_In,
  input  Calculate,
  input  Read,
  input  [1:0] Input_Select1,
  input  [31:0] Source1,
  input  [31:0] Program_Counter_In,
  input  [1:0] Input_Select2,
  input  [31:0] Source2,
  input  [31:0] Immediate_13bit,
  input  [31:0] Immediate_19bit,
  input  Clock,
  input  Reset,
  output [31:0] Result,
  output Zero,
  output Negative,
  output Overflow,
  output Carry_Out
);

  wire adder_1_cout, and_1_out, not_1_out, subtractor_1_bout;
  wire [30:0] C_q;
  wire [31:0] adder_1_out, and_2_out, multiplexer_1_out, multiplexer_2_out, multiplexer_3_out,
       multiplexer_4_out, multiplexer_6_out, or_1_out, S1_q, S2_q, subtractor_1_out, xor_1_out;

  not not_1 (not_1_out, Clock);
  Multiplexer #(.select(2), .width(32)) multiplexer_1 (
    .in0(Source1), .in1(Program_Counter_In), .in2(Program_Counter_In), .in3({32{1'b0}}),
    .out(multiplexer_1_out), .sel(Input_Select1));
  Multiplexer #(.select(2), .width(32)) multiplexer_2 (
    .in0(Source2), .in1(Immediate_13bit), .in2(Immediate_19bit), .in3(Immediate_19bit),
    .out(multiplexer_2_out), .sel(Input_Select2));
  Register #(.width(32)) S1 (.D(multiplexer_1_out), .en(Write), .clk(not_1_out), .Q(S1_q), .clr(Reset));
  Register #(.width(32)) S2 (.D(multiplexer_2_out), .en(Write), .clk(not_1_out), .Q(S2_q), .clr(Reset));
  // Probe on S1_q
  // Probe on S2_q
  Multiplexer #(.width(32)) multiplexer_3 (.in0(S1_q), .in1(S2_q), .out(multiplexer_3_out), .sel(Operation[3]));
  Multiplexer #(.width(32)) multiplexer_4 (.in0(S2_q), .in1(S1_q), .out(multiplexer_4_out), .sel(Operation[3]));
  and and_1 (and_1_out, Carry_In, Operation[0]);
  assign and_2_out = multiplexer_3_out & multiplexer_4_out;  // AND_Gate and_2, 32 bits wide
  assign xor_1_out = multiplexer_3_out ^ multiplexer_4_out;  // XOR_Gate xor_1, 32 bits wide
  assign or_1_out = multiplexer_3_out | multiplexer_4_out;  // OR_Gate or_1, 32 bits wide
  Subtractor #(.width(32)) subtractor_1 (
    .a(multiplexer_3_out), .b(multiplexer_4_out), .out(subtractor_1_out), .bin(and_1_out),
    .bout(subtractor_1_bout));
  Adder #(.width(32)) adder_1 (
    .a(multiplexer_3_out), .b(multiplexer_4_out), .out(adder_1_out), .cin(and_1_out), .cout(adder_1_cout));
  Multiplexer multiplexer_5 (.in0(subtractor_1_bout), .in1(adder_1_cout), .out(Carry_Out), .sel(Operation[1]));
  Multiplexer #(.select(3), .width(32)) multiplexer_6 (
    .in0(multiplexer_4_out), .in1(and_2_out), .in2(xor_1_out), .in3(or_1_out), .in4(subtractor_1_out),
    .in5(subtractor_1_out), .in6(adder_1_out), .in7(adder_1_out), .out(multiplexer_6_out),
    .sel(Operation[2:0]));
  Register #(.width(32)) C (.D(multiplexer_6_out), .en(Calculate), .clk(not_1_out), .Q({Negative, C_q}), .clr(Reset));
  nor nor_1 (Zero, C_q[0], C_q[1], C_q[2], C_q[3], C_q[4], C_q[5], C_q[6], C_q[7], C_q[8], C_q[9], C_q[10], C_q[11], C_q[12], C_q[13], C_q[14], C_q[15], C_q[16], C_q[17], C_q[18], C_q[19], C_q[20], C_q[21], C_q[22], C_q[23], C_q[24], C_q[25], C_q[26], C_q[27], C_q[28], C_q[29], C_q[30], Negative);
  xor xor_2 (Overflow, Negative, Carry_Out);
  assign Result = Read ? {Negative, C_q} : 32'bz;  // Controlled_Buffer controlled_buffer_1

  // Notes on the sheet:
  //   Source1: initial=0xffffffff
endmodule

module Program_Counter (
  input  Load_Interrupt_Vector,
  input  Write_Next,
  input  Write_Current,
  input  Write_Last,
  input  Reset,
  input  Clock,
  input  Enable_Current_Out,
  input  Enable_Last_Out,
  input  Enable_D_In,
  input  Next_P_Out,
  input  [31:0] D_Bus_In,
  input  D_Bus_To_P,
  input  Use_Offset,
  output [31:0] C_Bus_Out,
  output [31:0] Program_Counter_Out,
  output [31:0] P_Bus_Out,
  output [1:0] Byte_Offset
);

  wire not_1_out;
  wire [1:0] and_1_out;
  wire [29:0] adder_1_out, controlled_buffer_1_out, Last_q, multiplexer_1_out, Next_PC_q;

  Adder #(.width(30)) adder_1 (.a(Next_PC_q), .b(30'h1), .out(adder_1_out));  // open: cin, cout
  assign controlled_buffer_1_out = not_1_out ? multiplexer_1_out : 30'bz;  // Controlled_Buffer controlled_buffer_1
  Multiplexer #(.width(30)) multiplexer_1 (
    .in0(adder_1_out), .in1(30'h20000000), .out(multiplexer_1_out), .sel(Load_Interrupt_Vector));
  not not_1 (not_1_out, Enable_D_In);
  Register #(.width(30)) Next_PC (
    .D(controlled_buffer_1_out), .en(Write_Next), .clk(Clock), .Q(Next_PC_q), .clr(Reset));
  assign controlled_buffer_1_out = Enable_D_In ? D_Bus_In[31:2] : 30'bz;  // Controlled_Buffer controlled_buffer_2
  assign and_1_out = {2{Use_Offset}} & Byte_Offset;  // AND_Gate and_1, 2 bits wide
  assign P_Bus_Out = Next_P_Out ? {Next_PC_q, 2'b00} : 32'bz;  // Controlled_Buffer controlled_buffer_3
  assign P_Bus_Out = D_Bus_To_P ? {D_Bus_In[31:2], and_1_out} : 32'bz;  // Controlled_Buffer controlled_buffer_4
  Register #(.width(2)) Byte_Select_Latch (
    .D(D_Bus_In[1:0]), .en(D_Bus_To_P), .clk(Clock), .Q(Byte_Offset), .clr(Reset));
  Register #(.width(30)) Current (
    .D(Next_PC_q), .en(Write_Current), .clk(Clock), .Q(Program_Counter_Out[31:2]), .clr(Reset));
  assign C_Bus_Out = Enable_Current_Out ? {Program_Counter_Out[31:2], 2'b00} : 32'bz;  // Controlled_Buffer controlled_buffer_5
  Register #(.width(30)) Last (.D(Program_Counter_Out[31:2]), .en(Write_Last), .clk(Clock), .Q(Last_q), .clr(Reset));
  assign C_Bus_Out = Enable_Last_Out ? {Last_q, 2'b00} : 32'bz;  // Controlled_Buffer controlled_buffer_6

  assign Program_Counter_Out[1:0] = 2'b00;
endmodule

module Immediate_Register (
  input  [31:0] Pbus_In,
  input  Write_Enable,
  input  Clock,
  input  Reset,
  input  LoadHigh,
  output [4:0] Shift_Amount,
  output Immediate_Flag,
  output [31:0] Immediate_13bit,
  output [31:0] Immediate_19bit
);

  wire [4:0] register_1_q_2;
  wire [12:5] register_1_q;
  wire [31:0] bit_extender_2_out;

  Register #(.width(19)) register_1 (
    .D(Pbus_In[18:0]), .en(Write_Enable), .clk(Clock),
    .Q({register_1_q_2, Immediate_Flag, register_1_q, Shift_Amount}), .clr(Reset));
  assign Immediate_13bit = {{19{register_1_q[12]}}, {register_1_q, Shift_Amount}};  // Bit_Extender bit_extender_1
  assign bit_extender_2_out = {{13{register_1_q_2[4]}}, {register_1_q_2, Immediate_Flag, register_1_q, Shift_Amount}};  // Bit_Extender bit_extender_2
  Multiplexer #(.width(32)) multiplexer_1 (
    .in0(bit_extender_2_out), .in1({register_1_q_2, Immediate_Flag, register_1_q, Shift_Amount, {13{1'b0}}}),
    .out(Immediate_19bit), .sel(LoadHigh));
endmodule

module Shifter_Circuit (
  input  Select_Byte_Control,
  input  Select_Immediate,
  input  [31:0] B_Bus_In,
  input  [4:0] Immediate_In,
  input  [1:0] Byte_Control_In,
  input  Enable_C_Out,
  input  [1:0] Operation_Select,
  input  Write,
  input  [31:0] A_Bus_In,
  input  Enable_L_Out,
  input  [31:0] LBus_In,
  input  Enable_L_In,
  input  Calculate,
  input  Clock,
  output [31:0] C_Bus_Out,
  output [31:0] LBus_Out
);

  wire not_1_out;
  wire [4:0] multiplexer_1_out, multiplexer_2_out, Shift_Amount_Latch_q;
  wire [31:0] multiplexer_3_out, multiplexer_4_out, Shift_In_Latch_q, Shift_Out_Latch_q, shifter_1_out,
       shifter_2_out, shifter_3_out;

  Multiplexer #(.width(5)) multiplexer_1 (
    .in0(B_Bus_In[4:0]), .in1(Immediate_In), .out(multiplexer_1_out), .sel(Select_Immediate));
  Multiplexer #(.width(5)) multiplexer_2 (
    .in0(multiplexer_1_out), .in1({Byte_Control_In, 3'b000}), .out(multiplexer_2_out),
    .sel(Select_Byte_Control));
  not not_1 (not_1_out, Clock);
  Register #(.width(5)) Shift_Amount_Latch (
    .D(multiplexer_2_out), .en(Write), .clk(not_1_out), .Q(Shift_Amount_Latch_q));  // open: clr
  Register #(.width(32)) Shift_In_Latch (.D(A_Bus_In), .en(Write), .clk(not_1_out), .Q(Shift_In_Latch_q));  // open: clr
  assign LBus_Out = Enable_L_Out ? Shift_In_Latch_q : 32'bz;  // Controlled_Buffer controlled_buffer_1
  Multiplexer #(.width(32)) multiplexer_3 (
    .in0(Shift_In_Latch_q), .in1(LBus_In), .out(multiplexer_3_out), .sel(Enable_L_In));
  Shifter #(.width(32)) shifter_1 (.in(multiplexer_3_out), .\dist (Shift_Amount_Latch_q), .out(shifter_1_out));
  Shifter #(.shift("lr"), .width(32)) shifter_2 (
    .in(multiplexer_3_out), .\dist (Shift_Amount_Latch_q), .out(shifter_2_out));
  Shifter #(.shift("ar"), .width(32)) shifter_3 (
    .in(multiplexer_3_out), .\dist (Shift_Amount_Latch_q), .out(shifter_3_out));
  Multiplexer #(.select(2), .width(32)) multiplexer_4 (
    .in0(shifter_1_out), .in1(shifter_2_out), .in2(shifter_3_out), .in3(shifter_3_out),
    .out(multiplexer_4_out), .sel(Operation_Select));
  Register #(.width(32)) Shift_Out_Latch (
    .D(multiplexer_4_out), .en(Calculate), .clk(Clock), .Q(Shift_Out_Latch_q));  // open: clr
  assign C_Bus_Out = Enable_C_Out ? Shift_Out_Latch_q : 32'bz;  // Controlled_Buffer controlled_buffer_2
endmodule

module Data_Input_Output (
  input  Read_To_P,
  input  Write_From_P,
  input  Signed_Data,
  input  [1:0] Data_Size,
  input  Write_From_L,
  input  [1:0] Data_Offset,
  input  Read_To_L,
  input  [31:0] PBus_In,
  input  [31:0] LBus_In,
  input  Clock,
  output [31:0] PBus_Out,
  output [31:0] Lbus_Out
);

  wire and_1_out, and_2_out, and_3_out, or_1_out;
  wire [2:0] byte_decoder_1_mux_enables;
  wire [7:0] bit_extender_1_out, bit_extender_2_out, bit_extender_3_out, multiplexer_1_out,
       multiplexer_2_out, multiplexer_3_out, multiplexer_4_out, multiplexer_5_out, multiplexer_6_out,
       multiplexer_7_out, register_1_q, register_2_q, register_3_q, register_4_q;
  wire [31:0] controlled_buffer_2_out, controlled_buffer_7_out;

  assign PBus_Out = Read_To_P ? controlled_buffer_2_out : 32'bz;  // Controlled_Buffer controlled_buffer_1
  assign controlled_buffer_2_out = Write_From_P ? PBus_In : 32'bz;  // Controlled_Buffer controlled_buffer_2
  assign controlled_buffer_2_out[7:0] = Read_To_P ? register_1_q : 8'bz;  // Controlled_Buffer controlled_buffer_3
  assign controlled_buffer_2_out[15:8] = Read_To_P ? register_2_q : 8'bz;  // Controlled_Buffer controlled_buffer_4
  assign controlled_buffer_2_out[23:16] = Read_To_P ? register_3_q : 8'bz;  // Controlled_Buffer controlled_buffer_5
  assign controlled_buffer_2_out[31:24] = Read_To_P ? register_4_q : 8'bz;  // Controlled_Buffer controlled_buffer_6
  Multiplexer #(.width(8)) multiplexer_1 (
    .in0(controlled_buffer_2_out[7:0]), .in1(controlled_buffer_7_out[7:0]), .out(multiplexer_1_out),
    .sel(Write_From_L));
  Multiplexer #(.width(8)) multiplexer_2 (
    .in0(controlled_buffer_2_out[15:8]), .in1(controlled_buffer_7_out[15:8]), .out(multiplexer_2_out),
    .sel(Write_From_L));
  Multiplexer #(.width(8)) multiplexer_3 (
    .in0(controlled_buffer_2_out[23:16]), .in1(controlled_buffer_7_out[23:16]), .out(multiplexer_3_out),
    .sel(Write_From_L));
  Multiplexer #(.width(8)) multiplexer_4 (
    .in0(controlled_buffer_2_out[31:24]), .in1(controlled_buffer_7_out[31:24]), .out(multiplexer_4_out),
    .sel(Write_From_L));
  or or_1 (or_1_out, Write_From_P, Write_From_L);
  Register register_1 (.D(multiplexer_1_out), .en(or_1_out), .clk(Clock), .Q(register_1_q));  // open: clr
  Register register_2 (.D(multiplexer_2_out), .en(or_1_out), .clk(Clock), .Q(register_2_q));  // open: clr
  Register register_3 (.D(multiplexer_3_out), .en(or_1_out), .clk(Clock), .Q(register_3_q));  // open: clr
  Register register_4 (.D(multiplexer_4_out), .en(or_1_out), .clk(Clock), .Q(register_4_q));  // open: clr
  and and_1 (and_1_out, Signed_Data, register_1_q[7]);
  and and_2 (and_2_out, Signed_Data, multiplexer_5_out[7]);
  and and_3 (and_3_out, Signed_Data, multiplexer_6_out[7]);
  assign bit_extender_1_out = {{7{and_1_out}}, and_1_out};  // Bit_Extender bit_extender_1
  Multiplexer #(.width(8)) multiplexer_5 (
    .in0(bit_extender_1_out), .in1(register_2_q), .out(multiplexer_5_out), .sel(byte_decoder_1_mux_enables[0]));
  assign bit_extender_2_out = {{7{and_2_out}}, and_2_out};  // Bit_Extender bit_extender_2
  Multiplexer #(.width(8)) multiplexer_6 (
    .in0(bit_extender_2_out), .in1(register_3_q), .out(multiplexer_6_out), .sel(byte_decoder_1_mux_enables[1]));
  assign bit_extender_3_out = {{7{and_3_out}}, and_3_out};  // Bit_Extender bit_extender_3
  Multiplexer #(.width(8)) multiplexer_7 (
    .in0(bit_extender_3_out), .in1(register_4_q), .out(multiplexer_7_out), .sel(byte_decoder_1_mux_enables[2]));
  Byte_Decoder byte_decoder_1 (
    .Data_Size(Data_Size), .Data_Offset(Data_Offset), .Mux_Enables(byte_decoder_1_mux_enables));
  assign controlled_buffer_7_out[7:0] = Read_To_L ? register_1_q : 8'bz;  // Controlled_Buffer controlled_buffer_7
  assign controlled_buffer_7_out[15:8] = Read_To_L ? multiplexer_5_out : 8'bz;  // Controlled_Buffer controlled_buffer_8
  assign controlled_buffer_7_out[23:16] = Read_To_L ? multiplexer_6_out : 8'bz;  // Controlled_Buffer controlled_buffer_9
  assign controlled_buffer_7_out[31:24] = Read_To_L ? multiplexer_7_out : 8'bz;  // Controlled_Buffer controlled_buffer_10
  assign Lbus_Out = Read_To_L ? controlled_buffer_7_out : 32'bz;  // Controlled_Buffer controlled_buffer_11
  assign controlled_buffer_7_out = Write_From_L ? LBus_In : 32'bz;  // Controlled_Buffer controlled_buffer_12

  // Notes on the sheet:
  //   LBus_In: initial=0xe3e3e3e3
  //   PBus_In: initial=0xf2f2f2f2
endmodule

module Register_File (
  input  Write_Current_Adresses,
  input  Write_C_Address_To_A,
  input  [31:0] P_Bus_in,
  input  Write_Next_Addresses,
  input  Write_Interrupt_Register,
  input  [31:0] C_Bus_In,
  input  [2:0] Window_Number,
  input  Read,
  input  Write,
  input  Reset,
  input  Clock,
  output [31:0] A_Bus_Out,
  output [31:0] B_Bus_Out
);

  wire or_1_out, or_2_out;
  wire [2:0] A_Address_q_2, and_1_out, cwp_and_address_decoder_1_decoded_enables,
       cwp_and_address_decoder_1_decoded_enables_2, cwp_and_address_decoder_1_decoded_enables_3,
       cwp_and_address_decoder_1_decoded_enables_4, cwp_and_address_decoder_1_decoded_enables_5,
       cwp_and_address_decoder_1_decoded_enables_6, cwp_and_address_decoder_1_decoded_enables_7,
       cwp_and_address_decoder_1_decoded_enables_8;
  wire [3:0] A_Address_q, B_Address_q, C_Address_q;
  wire [4:0] multiplexer_1_out, multiplexer_2_out, Next_A_q, Next_B_q, Next_C_q;

  Multiplexer #(.width(5)) multiplexer_1 (
    .in0(P_Bus_in[23:19]), .in1(5'b11001), .out(multiplexer_1_out), .sel(Write_Interrupt_Register));
  Register #(.trigger("high"), .width(5)) Next_A (
    .D(P_Bus_in[18:14]), .en(Write_Next_Addresses), .clk(Clock), .Q(Next_A_q), .clr(Reset));
  Register #(.trigger("high"), .width(5)) Next_B (
    .D(P_Bus_in[4:0]), .en(Write_Next_Addresses), .clk(Clock), .Q(Next_B_q), .clr(Reset));
  Register #(.trigger("high"), .width(5)) Next_C (
    .D(multiplexer_1_out), .en(or_1_out), .clk(Clock), .Q(Next_C_q), .clr(Reset));
  or or_1 (or_1_out, Write_Interrupt_Register, Write_Next_Addresses);
  Multiplexer #(.width(5)) multiplexer_2 (
    .in0(Next_A_q), .in1({A_Address_q_2[2], C_Address_q}), .out(multiplexer_2_out), .sel(Write_C_Address_To_A));
  or or_2 (or_2_out, Write_C_Address_To_A, Write_Current_Adresses);
  Register #(.trigger("high"), .width(5)) A_Address (
    .D(multiplexer_2_out), .en(or_2_out), .clk(Clock), .Q({A_Address_q_2[0], A_Address_q}), .clr(Reset));
  Register #(.trigger("high"), .width(5)) B_Address (
    .D(Next_B_q), .en(Write_Current_Adresses), .clk(Clock), .Q({A_Address_q_2[1], B_Address_q}), .clr(Reset));
  Register #(.trigger("high"), .width(5)) C_Address (
    .D(Next_C_q), .en(Write_Current_Adresses), .clk(Clock), .Q({A_Address_q_2[2], C_Address_q}), .clr(Reset));
  CWP_And_Address_Decoder cwp_and_address_decoder_1 (
    .A_Address({A_Address_q_2[0], A_Address_q}), .B_Address({A_Address_q_2[1], B_Address_q}),
    .C_Address({A_Address_q_2[2], C_Address_q}), .Enable_Write(Write), .Enable_Read(Read),
    .Context_Window_Pointer(Window_Number),
    .Decoded_Enables({cwp_and_address_decoder_1_decoded_enables_8, cwp_and_address_decoder_1_decoded_enables_7, cwp_and_address_decoder_1_decoded_enables_6, cwp_and_address_decoder_1_decoded_enables_5, cwp_and_address_decoder_1_decoded_enables_4, cwp_and_address_decoder_1_decoded_enables_3, cwp_and_address_decoder_1_decoded_enables_2, cwp_and_address_decoder_1_decoded_enables}));
  assign and_1_out = ~A_Address_q_2 & {Write, {2{Read}}};  // AND_Gate and_1, 3 bits wide
  Register_Window register_window_1 (
    .Address_A(A_Address_q), .Address_B(B_Address_q),
    .Read_Enable_A(cwp_and_address_decoder_1_decoded_enables_8[0]),
    .Read_Enable_B(cwp_and_address_decoder_1_decoded_enables_8[1]), .Data_In(C_Bus_In), .Clock(Clock),
    .Address_C(C_Address_q), .Write_Enable(cwp_and_address_decoder_1_decoded_enables_8[2]), .Reset(Reset),
    .A_Data_Out(A_Bus_Out), .B_Data_Out(B_Bus_Out));
  Register_Window register_window_2 (
    .Address_A(A_Address_q), .Address_B(B_Address_q),
    .Read_Enable_A(cwp_and_address_decoder_1_decoded_enables_6[0]),
    .Read_Enable_B(cwp_and_address_decoder_1_decoded_enables_6[1]), .Data_In(C_Bus_In), .Clock(Clock),
    .Address_C(C_Address_q), .Write_Enable(cwp_and_address_decoder_1_decoded_enables_6[2]), .Reset(Reset),
    .A_Data_Out(A_Bus_Out), .B_Data_Out(B_Bus_Out));
  Register_Window register_window_3 (
    .Address_A(A_Address_q), .Address_B(B_Address_q),
    .Read_Enable_A(cwp_and_address_decoder_1_decoded_enables_4[0]),
    .Read_Enable_B(cwp_and_address_decoder_1_decoded_enables_4[1]), .Data_In(C_Bus_In), .Clock(Clock),
    .Address_C(C_Address_q), .Write_Enable(cwp_and_address_decoder_1_decoded_enables_4[2]), .Reset(Reset),
    .A_Data_Out(A_Bus_Out), .B_Data_Out(B_Bus_Out));
  Register_Window register_window_4 (
    .Address_A(A_Address_q), .Address_B(B_Address_q),
    .Read_Enable_A(cwp_and_address_decoder_1_decoded_enables_2[0]),
    .Read_Enable_B(cwp_and_address_decoder_1_decoded_enables_2[1]), .Data_In(C_Bus_In), .Clock(Clock),
    .Address_C(C_Address_q), .Write_Enable(cwp_and_address_decoder_1_decoded_enables_2[2]), .Reset(Reset),
    .A_Data_Out(A_Bus_Out), .B_Data_Out(B_Bus_Out));
  Global_Registers global_registers_1 (
    .Address_A(A_Address_q), .Address_B(B_Address_q), .Read_Enable_A(and_1_out[0]),
    .Read_Enable_B(and_1_out[1]), .Reset(Reset), .Data_In(C_Bus_In), .Address_C(C_Address_q),
    .Write_Enable(and_1_out[2]), .Clock(Clock), .A_Data_Out(A_Bus_Out), .B_Data_Out(B_Bus_Out));
  Register_Window register_window_5 (
    .Address_A(A_Address_q), .Address_B(B_Address_q),
    .Read_Enable_A(cwp_and_address_decoder_1_decoded_enables_7[0]),
    .Read_Enable_B(cwp_and_address_decoder_1_decoded_enables_7[1]), .Data_In(C_Bus_In), .Clock(Clock),
    .Address_C(C_Address_q), .Write_Enable(cwp_and_address_decoder_1_decoded_enables_7[2]), .Reset(Reset),
    .A_Data_Out(A_Bus_Out), .B_Data_Out(B_Bus_Out));
  Register_Window register_window_6 (
    .Address_A(A_Address_q), .Address_B(B_Address_q),
    .Read_Enable_A(cwp_and_address_decoder_1_decoded_enables_5[0]),
    .Read_Enable_B(cwp_and_address_decoder_1_decoded_enables_5[1]), .Data_In(C_Bus_In), .Clock(Clock),
    .Address_C(C_Address_q), .Write_Enable(cwp_and_address_decoder_1_decoded_enables_5[2]), .Reset(Reset),
    .A_Data_Out(A_Bus_Out), .B_Data_Out(B_Bus_Out));
  Register_Window register_window_7 (
    .Address_A(A_Address_q), .Address_B(B_Address_q),
    .Read_Enable_A(cwp_and_address_decoder_1_decoded_enables_3[0]),
    .Read_Enable_B(cwp_and_address_decoder_1_decoded_enables_3[1]), .Data_In(C_Bus_In), .Clock(Clock),
    .Address_C(C_Address_q), .Write_Enable(cwp_and_address_decoder_1_decoded_enables_3[2]), .Reset(Reset),
    .A_Data_Out(A_Bus_Out), .B_Data_Out(B_Bus_Out));
  Register_Window register_window_8 (
    .Address_A(A_Address_q), .Address_B(B_Address_q),
    .Read_Enable_A(cwp_and_address_decoder_1_decoded_enables[0]),
    .Read_Enable_B(cwp_and_address_decoder_1_decoded_enables[1]), .Data_In(C_Bus_In), .Clock(Clock),
    .Address_C(C_Address_q), .Write_Enable(cwp_and_address_decoder_1_decoded_enables[2]), .Reset(Reset),
    .A_Data_Out(A_Bus_Out), .B_Data_Out(B_Bus_Out));
endmodule

module Register_Window (
  input  [3:0] Address_A,
  input  Read_Enable_A,
  input  Reset,
  input  [31:0] Data_In,
  input  Clock,
  input  [3:0] Address_C,
  input  Write_Enable,
  input  [3:0] Address_B,
  input  Read_Enable_B,
  output [31:0] A_Data_Out,
  output [31:0] B_Data_Out
);

  wire decoder_1_out0, decoder_1_out1, decoder_1_out2, decoder_1_out3, decoder_1_out4, decoder_1_out5,
       decoder_1_out6, decoder_1_out7, decoder_1_out8, decoder_1_out9, decoder_1_out10, decoder_1_out11,
       decoder_1_out12, decoder_1_out13, decoder_1_out14, decoder_1_out15;
  wire [31:0] Reg0_q, Reg1_q, Reg2_q, Reg3_q, Reg4_q, Reg5_q, Reg6_q, Reg7_q, Reg8_q, Reg9_q, RegA_q, RegB_q,
       RegC_q, RegD_q, RegE_q, RegF_q;

  Decoder #(.select(4)) decoder_1 (
    .out0(decoder_1_out0), .out1(decoder_1_out1), .out2(decoder_1_out2), .out3(decoder_1_out3),
    .out4(decoder_1_out4), .out5(decoder_1_out5), .out6(decoder_1_out6), .out7(decoder_1_out7),
    .out8(decoder_1_out8), .out9(decoder_1_out9), .out10(decoder_1_out10), .out11(decoder_1_out11),
    .out12(decoder_1_out12), .out13(decoder_1_out13), .out14(decoder_1_out14), .out15(decoder_1_out15),
    .sel(Address_C), .en(Write_Enable));
  Register #(.width(32)) Reg0 (.D(Data_In), .en(decoder_1_out0), .clk(Clock), .Q(Reg0_q), .clr(Reset));
  Register #(.width(32)) Reg2 (.D(Data_In), .en(decoder_1_out2), .clk(Clock), .Q(Reg2_q), .clr(Reset));
  Register #(.width(32)) Reg4 (.D(Data_In), .en(decoder_1_out4), .clk(Clock), .Q(Reg4_q), .clr(Reset));
  Register #(.width(32)) Reg6 (.D(Data_In), .en(decoder_1_out6), .clk(Clock), .Q(Reg6_q), .clr(Reset));
  Register #(.width(32)) Reg8 (.D(Data_In), .en(decoder_1_out8), .clk(Clock), .Q(Reg8_q), .clr(Reset));
  Register #(.width(32)) RegA (.D(Data_In), .en(decoder_1_out10), .clk(Clock), .Q(RegA_q), .clr(Reset));
  Register #(.width(32)) RegC (.D(Data_In), .en(decoder_1_out12), .clk(Clock), .Q(RegC_q), .clr(Reset));
  Register #(.width(32)) RegE (.D(Data_In), .en(decoder_1_out14), .clk(Clock), .Q(RegE_q), .clr(Reset));
  Register #(.width(32)) Reg1 (.D(Data_In), .en(decoder_1_out1), .clk(Clock), .Q(Reg1_q), .clr(Reset));
  Register #(.width(32)) Reg3 (.D(Data_In), .en(decoder_1_out3), .clk(Clock), .Q(Reg3_q), .clr(Reset));
  Register #(.width(32)) Reg5 (.D(Data_In), .en(decoder_1_out5), .clk(Clock), .Q(Reg5_q), .clr(Reset));
  Register #(.width(32)) Reg7 (.D(Data_In), .en(decoder_1_out7), .clk(Clock), .Q(Reg7_q), .clr(Reset));
  Register #(.width(32)) Reg9 (.D(Data_In), .en(decoder_1_out9), .clk(Clock), .Q(Reg9_q), .clr(Reset));
  Register #(.width(32)) RegB (.D(Data_In), .en(decoder_1_out11), .clk(Clock), .Q(RegB_q), .clr(Reset));
  Register #(.width(32)) RegD (.D(Data_In), .en(decoder_1_out13), .clk(Clock), .Q(RegD_q), .clr(Reset));
  Register #(.width(32)) RegF (.D(Data_In), .en(decoder_1_out15), .clk(Clock), .Q(RegF_q), .clr(Reset));
  Multiplexer #(.disabled("Z"), .enable("true"), .select(4), .width(32)) multiplexer_1 (
    .in0(Reg0_q), .in1(Reg1_q), .in2(Reg2_q), .in3(Reg3_q), .in4(Reg4_q), .in5(Reg5_q), .in6(Reg6_q),
    .in7(Reg7_q), .in8(Reg8_q), .in9(Reg9_q), .in10(RegA_q), .in11(RegB_q), .in12(RegC_q), .in13(RegD_q),
    .in14(RegE_q), .in15(RegF_q), .out(A_Data_Out), .sel(Address_A), .en(Read_Enable_A));
  Multiplexer #(.disabled("Z"), .enable("true"), .select(4), .width(32)) multiplexer_2 (
    .in0(Reg0_q), .in1(Reg1_q), .in2(Reg2_q), .in3(Reg3_q), .in4(Reg4_q), .in5(Reg5_q), .in6(Reg6_q),
    .in7(Reg7_q), .in8(Reg8_q), .in9(Reg9_q), .in10(RegA_q), .in11(RegB_q), .in12(RegC_q), .in13(RegD_q),
    .in14(RegE_q), .in15(RegF_q), .out(B_Data_Out), .sel(Address_B), .en(Read_Enable_B));
endmodule

module Global_Registers (
  input  [3:0] Address_A,
  input  Read_Enable_A,
  input  Reset,
  input  [31:0] Data_In,
  input  Clock,
  input  [3:0] Address_C,
  input  Write_Enable,
  input  [3:0] Address_B,
  input  Read_Enable_B,
  output [31:0] A_Data_Out,
  output [31:0] B_Data_Out
);

  wire decoder_1_out0, decoder_1_out1, decoder_1_out2, decoder_1_out3, decoder_1_out4, decoder_1_out5,
       decoder_1_out6, decoder_1_out7, decoder_1_out8, decoder_1_out9, decoder_1_out10, decoder_1_out11,
       decoder_1_out12, decoder_1_out13, decoder_1_out14, decoder_1_out15;
  wire [31:0] Reg1_q, Reg2_q, Reg3_q, Reg4_q, Reg5_q, Reg6_q, Reg7_q, Reg8_q, Reg9_q, undriven, undriven_2,
       undriven_3, undriven_4, undriven_5, undriven_6;

  Decoder #(.select(4)) decoder_1 (
    .out0(decoder_1_out0), .out1(decoder_1_out1), .out2(decoder_1_out2), .out3(decoder_1_out3),
    .out4(decoder_1_out4), .out5(decoder_1_out5), .out6(decoder_1_out6), .out7(decoder_1_out7),
    .out8(decoder_1_out8), .out9(decoder_1_out9), .out10(decoder_1_out10), .out11(decoder_1_out11),
    .out12(decoder_1_out12), .out13(decoder_1_out13), .out14(decoder_1_out14), .out15(decoder_1_out15),
    .sel(Address_C), .en(Write_Enable));
  // NoConnect on decoder_1_out15
  // NoConnect on decoder_1_out14
  // NoConnect on decoder_1_out13
  // NoConnect on decoder_1_out12
  // NoConnect on decoder_1_out11
  // NoConnect on decoder_1_out10
  // NoConnect on decoder_1_out0
  Register #(.width(32)) Reg2 (.D(Data_In), .en(decoder_1_out2), .clk(Clock), .Q(Reg2_q), .clr(Reset));
  Register #(.width(32)) Reg4 (.D(Data_In), .en(decoder_1_out4), .clk(Clock), .Q(Reg4_q), .clr(Reset));
  Register #(.width(32)) Reg6 (.D(Data_In), .en(decoder_1_out6), .clk(Clock), .Q(Reg6_q), .clr(Reset));
  Register #(.width(32)) Reg8 (.D(Data_In), .en(decoder_1_out8), .clk(Clock), .Q(Reg8_q), .clr(Reset));
  Register #(.width(32)) Reg1 (.D(Data_In), .en(decoder_1_out1), .clk(Clock), .Q(Reg1_q), .clr(Reset));
  Register #(.width(32)) Reg3 (.D(Data_In), .en(decoder_1_out3), .clk(Clock), .Q(Reg3_q), .clr(Reset));
  Register #(.width(32)) Reg5 (.D(Data_In), .en(decoder_1_out5), .clk(Clock), .Q(Reg5_q), .clr(Reset));
  Register #(.width(32)) Reg7 (.D(Data_In), .en(decoder_1_out7), .clk(Clock), .Q(Reg7_q), .clr(Reset));
  Register #(.width(32)) Reg9 (.D(Data_In), .en(decoder_1_out9), .clk(Clock), .Q(Reg9_q), .clr(Reset));
  // NoConnect on undriven
  // NoConnect on undriven_2
  // NoConnect on undriven_3
  // NoConnect on undriven_4
  // NoConnect on undriven_5
  // NoConnect on undriven_6
  Multiplexer #(.disabled("Z"), .enable("true"), .select(4), .width(32)) multiplexer_1 (
    .in0({32{1'b0}}), .in1(Reg1_q), .in2(Reg2_q), .in3(Reg3_q), .in4(Reg4_q), .in5(Reg5_q), .in6(Reg6_q),
    .in7(Reg7_q), .in8(Reg8_q), .in9(Reg9_q), .in10(undriven), .in11(undriven_2), .in12(undriven_3),
    .in13(undriven_4), .in14(undriven_5), .in15(undriven_6), .out(A_Data_Out), .sel(Address_A),
    .en(Read_Enable_A));
  Multiplexer #(.disabled("Z"), .enable("true"), .select(4), .width(32)) multiplexer_2 (
    .in0({32{1'b0}}), .in1(Reg1_q), .in2(Reg2_q), .in3(Reg3_q), .in4(Reg4_q), .in5(Reg5_q), .in6(Reg6_q),
    .in7(Reg7_q), .in8(Reg8_q), .in9(Reg9_q), .in10(undriven), .in11(undriven_2), .in12(undriven_3),
    .in13(undriven_4), .in14(undriven_5), .in15(undriven_6), .out(B_Data_Out), .sel(Address_B),
    .en(Read_Enable_B));

  // Notes on the sheet:
  //   Reg0
endmodule

module Operation_Controller (
  input  [31:0] P_Bus_In,
  input  [3:0] CNZV_In,
  input  Phase1n,
  input  Phase2n,
  input  Phase3n,
  input  Phase1s,
  input  Phase2s,
  input  Phase3s,
  input  Phase2i,
  input  Phase3i,
  input  Clock,
  input  Reset,
  output Set_Condition_Code,
  output Register_File_C_Address_To_A,
  output Select_High_Immediate,
  output ALU_Use_19bit_Immediate,
  output Relative,
  output Connect_D_C_Bus,
  output Alu_Read,
  output Shifter_Read_C,
  output Shifter_Write_L,
  output Shifter_Read_L,
  output Register_File_Write,
  output [3:0] ALU_Operation,
  output [1:0] Shift_Operation,
  output [1:0] Data_Size,
  output Signed_Load,
  output PC_Read_Current,
  output PC_Read_Last,
  output PC_Write_Next,
  output Window_Number_Write,
  output PC_Select_D_In,
  output Window_Number_Decrement,
  output PC_Use_Offset,
  output Window_Number_Increment,
  output PAD_Read,
  output Enable_Interrupt_Bit,
  output Interrupt_Call,
  output Data_IO_Store,
  output PAD_Write,
  output Data_IO_L_Read,
  output Status_Word_Write,
  output Load_Store,
  output Status_Word_Read
);

  wire ALU, and_11_out, and_12_out, and_15_out, and_16_out, and_17_out, and_22_out, and_24_out, and_25_out,
       and_26_out, and_27_out, Call, condition_decoder_1_always, condition_decoder_1_carry_clear,
       condition_decoder_1_carry_set, condition_decoder_1_equal, condition_decoder_1_greater,
       condition_decoder_1_greater_or_equal, condition_decoder_1_higher, condition_decoder_1_is_negative,
       condition_decoder_1_is_positive, condition_decoder_1_less, condition_decoder_1_less_or_equal,
       condition_decoder_1_lower_or_same, condition_decoder_1_never, condition_decoder_1_not_equal,
       condition_decoder_1_overflow_clear, condition_decoder_1_overflow_set, Condition_Valid, Get_Last_PC,
       Get_Processor_Status_Word, Interrupt_Instruction, Jump, Load, nor_1_out, or_1_out, or_2_out, or_3_out,
       or_4_out, or_5_out, or_8_out, or_9_out, or_10_out, or_11_out, ReturnInstruction,
       Set_Condition_Codes_q, Set_Processor_Status_Word, Shifter;
  wire [3:0] CNZV_q, Condition_Code_Select_q;
  wire [6:0] Operation_Code_q;
  wire [31:0] multiplexer_1_out, Next_Instruction_Word_q;

  Multiplexer #(.width(32)) multiplexer_1 (.in0(P_Bus_In), .in1(32'hc80000), .out(multiplexer_1_out), .sel(Phase2i));
  Register #(.width(32)) Next_Instruction_Word (
    .D(multiplexer_1_out), .en(or_1_out), .clk(Clock), .Q(Next_Instruction_Word_q));  // open: clr
  or or_1 (or_1_out, Phase2n, Phase2i);
  // Probe on Next_Instruction_Word_q
  Register #(.width(4)) CNZV (.D(CNZV_In), .en(Phase1n), .clk(Clock), .Q(CNZV_q));  // open: clr
  Register #(.width(7)) Operation_Code (
    .D(Next_Instruction_Word_q[31:25]), .en(Phase1n), .clk(Clock), .Q(Operation_Code_q), .clr(Reset));
  // Probe on Operation_Code_q
  Register #(.width(1)) Set_Condition_Codes (
    .D(Next_Instruction_Word_q[24]), .en(Phase1n), .clk(Clock), .Q(Set_Condition_Codes_q));  // open: clr
  Register #(.width(4)) Condition_Code_Select (
    .D(Next_Instruction_Word_q[22:19]), .en(Phase1n), .clk(Clock), .Q(Condition_Code_Select_q));  // open: clr
  Condition_Decoder condition_decoder_1 (
    .Carry_In(CNZV_q[3]), .Negative(CNZV_q[2]), .Zero(CNZV_q[1]), .Overflow(CNZV_q[0]),
    .Never(condition_decoder_1_never), .Always(condition_decoder_1_always),
    .Not_Equal(condition_decoder_1_not_equal), .Equal(condition_decoder_1_equal),
    .Greater(condition_decoder_1_greater), .Less_Or_Equal(condition_decoder_1_less_or_equal),
    .Greater_Or_Equal(condition_decoder_1_greater_or_equal), .Less(condition_decoder_1_less),
    .Is_Positive(condition_decoder_1_is_positive), .Is_Negative(condition_decoder_1_is_negative),
    .Higher(condition_decoder_1_higher), .Lower_Or_Same(condition_decoder_1_lower_or_same),
    .Overflow_Clear(condition_decoder_1_overflow_clear), .Overflow_Set(condition_decoder_1_overflow_set),
    .Carry_Clear(condition_decoder_1_carry_clear), .Carry_Set(condition_decoder_1_carry_set));
  Operation_Decoder operation_decoder_1 (
    .OPCODE(Operation_Code_q), .ALU_OP(ALU_Operation), .SHIFTER_OP(Shift_Operation), .BYTE_SIZE(Data_Size),
    .SIGNED(Signed_Load), .RELATIVE(Relative), .INTERRUPT(Interrupt_Instruction), .ALU(ALU),
    .SHIFTER(Shifter), .LOAD(Load), .STORE(PC_Use_Offset), .CALL(Call), .RETURN(ReturnInstruction),
    .JUMP(Jump), .GET_PSW(Get_Processor_Status_Word), .SET_PSW(Set_Processor_Status_Word),
    .GET_LAST_PC(Get_Last_PC), .LOAD_HIGH_IMMEDIATE(Select_High_Immediate));
  Multiplexer #(.select(4)) multiplexer_2 (
    .in0(condition_decoder_1_never), .in1(condition_decoder_1_greater),
    .in2(condition_decoder_1_less_or_equal), .in3(condition_decoder_1_greater_or_equal),
    .in4(condition_decoder_1_less), .in5(condition_decoder_1_higher),
    .in6(condition_decoder_1_lower_or_same), .in7(condition_decoder_1_carry_clear),
    .in8(condition_decoder_1_carry_set), .in9(condition_decoder_1_is_positive),
    .in10(condition_decoder_1_is_negative), .in11(condition_decoder_1_not_equal),
    .in12(condition_decoder_1_equal), .in13(condition_decoder_1_overflow_clear),
    .in14(condition_decoder_1_overflow_set), .in15(condition_decoder_1_always), .out(Condition_Valid),
    .sel(Condition_Code_Select_q));
  nor nor_1 (nor_1_out, Call, ReturnInstruction, Jump);
  and and_1 (Set_Condition_Code, nor_1_out, Set_Condition_Codes_q, Phase3n);
  and and_2 (Register_File_C_Address_To_A, PC_Use_Offset, Phase2n);
  or or_2 (or_2_out, Call, ReturnInstruction, Set_Processor_Status_Word);
  or or_3 (or_3_out, Phase2n, Phase1n);
  or or_4 (or_4_out, Select_High_Immediate, Get_Last_PC, Get_Processor_Status_Word, Load, Shifter, ALU, Call);
  and and_3 (Register_File_Write, Phase3n, or_4_out);
  and and_4 (Window_Number_Write, or_2_out, Phase2n);
  and and_5 (Window_Number_Decrement, ReturnInstruction, or_3_out);
  and and_6 (Window_Number_Increment, or_3_out, Call);
  and and_7 (Enable_Interrupt_Bit, Interrupt_Instruction, ReturnInstruction);
  and and_8 (Interrupt_Call, Interrupt_Instruction, Call);
  and and_9 (Status_Word_Write, Phase2n, Set_Processor_Status_Word);
  and and_10 (Status_Word_Read, Phase2n, Get_Processor_Status_Word);
  and and_11 (and_11_out, Phase3n, or_5_out);
  and and_12 (and_12_out, Jump, Condition_Valid);
  and and_13 (Data_IO_Store, Phase2s, PC_Use_Offset);
  and and_14 (Data_IO_L_Read, Phase2s, Load);
  or or_5 (or_5_out, Select_High_Immediate, Jump, ReturnInstruction, Call, ALU);
  or or_6 (Alu_Read, and_11_out, and_17_out);
  and and_15 (and_15_out, Call, Interrupt_Instruction);
  or or_7 (PC_Write_Next, Phase3i, Phase3n);
  and and_16 (and_16_out, ~Interrupt_Instruction, Call);  // AND_Gate
  or or_8 (or_8_out, PC_Use_Offset, Load);
  and and_17 (and_17_out, Phase3s, or_8_out);
  or or_9 (or_9_out, and_15_out, Get_Last_PC);
  or or_10 (or_10_out, and_16_out, ReturnInstruction, and_12_out);
  and and_18 (PC_Read_Current, Call, Phase3n, ~Interrupt_Instruction);  // AND_Gate
  and and_19 (PC_Read_Last, Phase3n, or_9_out);
  and and_20 (PC_Select_D_In, or_10_out, Phase3n);
  or or_11 (or_11_out, Shifter, Load, Get_Processor_Status_Word);
  and and_21 (Shifter_Read_C, Phase3n, or_11_out);
  or or_12 (PAD_Read, Phase2n, and_22_out);
  and and_22 (and_22_out, Load, Phase1s);
  and and_23 (PAD_Write, Phase2s, PC_Use_Offset);
  or or_13 (Load_Store, PC_Use_Offset, Load);
  and and_24 (and_24_out, Phase2n, Get_Processor_Status_Word);
  or or_14 (Shifter_Write_L, and_24_out, and_25_out);
  and and_25 (and_25_out, Phase2s, Load);
  and and_26 (and_26_out, Phase2n, Set_Processor_Status_Word);
  and and_27 (and_27_out, Phase2s, PC_Use_Offset);
  or or_15 (Shifter_Read_L, and_26_out, and_27_out);
  or or_16 (ALU_Use_19bit_Immediate, Select_High_Immediate, Relative);
  or or_17 (Connect_D_C_Bus, ALU, Select_High_Immediate);

  // Other names for the same wires on the sheet: Load_High_Immediate = Select_High_Immediate; Store = PC_Use_Offset

  // Notes on the sheet:
  //   Calli 25:
  //   Register File
  //   Interrupt
  //   Processor Status Word
  //   Window Controller
  //   Program Counter
  //   Input/Output and interface Pads
  //   ALU And Shifter
endmodule

module CWP_And_Address_Decoder (
  input  [4:0] A_Address,
  input  [4:0] B_Address,
  input  [4:0] C_Address,
  input  Enable_Write,
  input  Enable_Read,
  input  [2:0] Context_Window_Pointer,
  output [23:0] Decoded_Enables
);

  wire and_1_out, and_2_out, and_3_out, and_4_out, and_5_out, and_6_out, and_7_out, and_8_out, and_9_out,
       or_1_out, or_2_out, or_3_out;
  wire [2:0] and_12_out, and_15_out, demultiplexer_1_out0, demultiplexer_1_out1, demultiplexer_1_out2,
       demultiplexer_1_out3, demultiplexer_1_out4, demultiplexer_1_out5, demultiplexer_1_out6,
       demultiplexer_1_out7, demultiplexer_2_out0, demultiplexer_2_out1, demultiplexer_2_out2,
       demultiplexer_2_out3, demultiplexer_2_out4, demultiplexer_2_out5, demultiplexer_2_out6,
       demultiplexer_2_out7, subtractor_1_out;

  or or_1 (or_1_out, A_Address[1], A_Address[2]);
  and and_1 (and_1_out, A_Address[3], ~A_Address[4]);  // AND_Gate
  or or_2 (or_2_out, B_Address[1], B_Address[2]);
  and and_2 (and_2_out, B_Address[3], ~B_Address[4]);  // AND_Gate
  or or_3 (or_3_out, C_Address[1], C_Address[2]);
  and and_3 (and_3_out, C_Address[3], ~C_Address[4]);  // AND_Gate
  and and_4 (and_4_out, or_1_out, and_1_out);
  and and_5 (and_5_out, or_2_out, and_2_out);
  and and_6 (and_6_out, or_3_out, and_3_out);
  Subtractor #(.width(3)) subtractor_1 (
    .a(Context_Window_Pointer), .b(3'b001), .out(subtractor_1_out));  // open: bin, bout
  and and_7 (and_7_out, A_Address[4], ~and_4_out);  // AND_Gate
  and and_8 (and_8_out, B_Address[4], ~and_5_out);  // AND_Gate
  and and_9 (and_9_out, C_Address[4], ~and_6_out);  // AND_Gate
  and and_10 (and_12_out[2], and_9_out, Enable_Write);
  and and_11 (and_12_out[1], and_8_out, Enable_Read);
  and and_12 (and_12_out[0], and_7_out, Enable_Read);
  Demultiplexer #(.select(3), .width(3)) demultiplexer_1 (
    .out0(demultiplexer_1_out0), .out1(demultiplexer_1_out1), .out2(demultiplexer_1_out2),
    .out3(demultiplexer_1_out3), .out4(demultiplexer_1_out4), .out5(demultiplexer_1_out5),
    .out6(demultiplexer_1_out6), .out7(demultiplexer_1_out7), .in(and_12_out), .sel(Context_Window_Pointer));
  and and_13 (and_15_out[2], and_6_out, Enable_Write);
  and and_14 (and_15_out[1], and_5_out, Enable_Read);
  and and_15 (and_15_out[0], and_4_out, Enable_Read);
  Demultiplexer #(.select(3), .width(3)) demultiplexer_2 (
    .out0(demultiplexer_2_out0), .out1(demultiplexer_2_out1), .out2(demultiplexer_2_out2),
    .out3(demultiplexer_2_out3), .out4(demultiplexer_2_out4), .out5(demultiplexer_2_out5),
    .out6(demultiplexer_2_out6), .out7(demultiplexer_2_out7), .in(and_15_out), .sel(subtractor_1_out));
  assign Decoded_Enables = {demultiplexer_1_out7, demultiplexer_1_out6, demultiplexer_1_out5, demultiplexer_1_out4, demultiplexer_1_out3, demultiplexer_1_out2, demultiplexer_1_out1, demultiplexer_1_out0} | {demultiplexer_2_out7, demultiplexer_2_out6, demultiplexer_2_out5, demultiplexer_2_out4, demultiplexer_2_out3, demultiplexer_2_out2, demultiplexer_2_out1, demultiplexer_2_out0};  // OR_Gate or_4, 24 bits wide
  // Probe on {demultiplexer_1_out7, demultiplexer_1_out6, demultiplexer_1_out5, demultiplexer_1_out4, demultiplexer_1_out3, demultiplexer_1_out2, demultiplexer_1_out1, demultiplexer_1_out0}
  // Probe on {demultiplexer_2_out7, demultiplexer_2_out6, demultiplexer_2_out5, demultiplexer_2_out4, demultiplexer_2_out3, demultiplexer_2_out2, demultiplexer_2_out1, demultiplexer_2_out0}
  // Probe on Decoded_Enables

  // Notes on the sheet:
  //   is lower window address?
endmodule

module Window_Number_Controller (
  input  Read,
  input  [31:0] LBus_In,
  input  Clock,
  input  Write,
  input  Reset,
  input  Decrement_Window,
  input  Increment_Window,
  output [31:0] LBus_Out,
  output Window_Overflow,
  output [2:0] Window_Number
);

  wire and_1_out, comparator_1_eq, not_1_out, or_1_out, or_2_out;
  wire [2:0] adder_1_out, multiplexer_1_out, multiplexer_2_out, multiplexer_3_out, Next_Window_Pointer_q,
       subtractor_1_out;
  wire [6:4] Saved_Window_Pointer_q;

  not not_1 (not_1_out, Clock);
  assign LBus_Out = Read ? {{22{1'b0}}, Window_Number, Saved_Window_Pointer_q, 4'b0000} : 32'bz;  // Controlled_Buffer controlled_buffer_1
  and and_1 (and_1_out, Write, ~or_2_out);  // AND_Gate
  Multiplexer #(.width(3)) multiplexer_1 (
    .in0(LBus_In[9:7]), .in1(Next_Window_Pointer_q), .out(multiplexer_1_out), .sel(or_2_out));
  Multiplexer #(.width(3)) multiplexer_2 (.in0(LBus_In[6:4]), .in1(3'b111), .out(multiplexer_2_out), .sel(Reset));
  or or_1 (or_1_out, and_1_out, Reset);
  Register #(.width(3)) Saved_Window_Pointer (
    .D(multiplexer_2_out), .en(or_1_out), .clk(not_1_out), .Q(Saved_Window_Pointer_q));  // open: clr
  Register #(.width(3)) Current_Window_Pointer (
    .D(multiplexer_1_out), .en(Write), .clk(not_1_out), .Q(Window_Number), .clr(Reset));
  Adder #(.width(3)) adder_1 (.a(Window_Number), .b(3'b001), .out(adder_1_out));  // open: cin, cout
  Multiplexer #(.width(3)) multiplexer_3 (
    .in0(adder_1_out), .in1(subtractor_1_out), .out(multiplexer_3_out), .sel(Decrement_Window));
  Subtractor #(.width(3)) subtractor_1 (.a(Window_Number), .b(3'b001), .out(subtractor_1_out));  // open: bin, bout
  Comparator #(.mode("unsigned"), .width(3)) comparator_1 (
    .a(Saved_Window_Pointer_q), .b(multiplexer_3_out), .eq(comparator_1_eq));  // open: gt, lt
  or or_2 (or_2_out, Decrement_Window, Increment_Window);
  and and_2 (Window_Overflow, comparator_1_eq, or_2_out);
  Register #(.width(3)) Next_Window_Pointer (
    .D(multiplexer_3_out), .en(or_2_out), .clk(not_1_out), .Q(Next_Window_Pointer_q), .clr(Reset));
endmodule

module Operation_Decoder (
  input  [6:0] OPCODE,
  output [3:0] ALU_OP,
  output [1:0] SHIFTER_OP,
  output [1:0] BYTE_SIZE,
  output SIGNED,
  output RELATIVE,
  output INTERRUPT,
  output ALU,
  output SHIFTER,
  output LOAD,
  output STORE,
  output CALL,
  output RETURN,
  output JUMP,
  output GET_PSW,
  output SET_PSW,
  output GET_LAST_PC,
  output LOAD_HIGH_IMMEDIATE
);

  wire and_2_out, and_3_out, and_4_out, and_5_out, and_6_out, and_7_out, and_8_out, and_9_out, and_10_out,
       and_11_out, and_12_out, and_13_out, and_14_out, and_15_out, and_16_out, and_17_out, and_18_out,
       and_19_out, and_20_out, and_21_out, and_22_out, and_23_out, and_25_out, and_26_out, and_27_out,
       and_28_out, and_30_out, and_31_out, not_1_out, not_2_out, not_3_out, not_4_out, not_5_out, not_6_out;

  not not_1 (not_1_out, OPCODE[6]);
  not not_2 (not_2_out, OPCODE[5]);
  not not_3 (not_3_out, OPCODE[4]);
  not not_4 (not_4_out, OPCODE[3]);
  not not_5 (not_5_out, OPCODE[2]);
  not not_6 (not_6_out, OPCODE[1]);
  and and_1 (ALU_OP[3], OPCODE[6], not_2_out, OPCODE[4], not_4_out, OPCODE[2]);
  and and_2 (and_2_out, not_2_out, OPCODE[4]);
  and and_3 (and_3_out, OPCODE[5], not_3_out);
  and and_4 (and_4_out, not_3_out, OPCODE[2]);
  and and_5 (and_5_out, not_2_out, OPCODE[3]);
  and and_6 (and_6_out, OPCODE[5], not_3_out);
  and and_7 (and_7_out, OPCODE[6], not_2_out, not_3_out, not_5_out);
  and and_8 (and_8_out, OPCODE[6], not_2_out, OPCODE[3], OPCODE[2]);
  and and_9 (and_9_out, OPCODE[6], not_2_out, OPCODE[4], not_4_out, OPCODE[1]);
  and and_10 (and_10_out, not_1_out, OPCODE[5], not_3_out, OPCODE[2], OPCODE[1]);
  and and_11 (and_11_out, not_1_out, OPCODE[5], not_3_out, OPCODE[3], not_5_out);
  and and_12 (and_12_out, not_1_out, not_2_out, OPCODE[4], OPCODE[3], OPCODE[2]);
  and and_13 (and_13_out, not_1_out, OPCODE[5], not_3_out, OPCODE[2]);
  and and_14 (and_14_out, not_1_out, OPCODE[5], not_3_out, OPCODE[3]);
  and and_15 (and_15_out, not_1_out, not_2_out, OPCODE[4], OPCODE[3], not_5_out, not_6_out);
  and and_16 (and_16_out, not_3_out, not_5_out);
  and and_17 (and_17_out, OPCODE[4], OPCODE[3]);
  or or_1 (BYTE_SIZE[0], not_2_out, not_5_out, OPCODE[3], OPCODE[6]);
  or or_2 (SIGNED, not_2_out, not_5_out, OPCODE[1], OPCODE[4], OPCODE[6]);
  and and_18 (and_18_out, not_1_out, OPCODE[5], OPCODE[2], OPCODE[0]);
  and and_19 (and_19_out, not_1_out, OPCODE[5], OPCODE[3], OPCODE[0]);
  and and_20 (and_20_out, not_1_out, not_2_out, not_3_out, OPCODE[3], OPCODE[2]);
  and and_21 (and_21_out, not_1_out, OPCODE[5], OPCODE[4], OPCODE[0]);
  and and_22 (and_22_out, not_1_out, not_2_out, not_3_out, not_4_out);
  and and_23 (and_23_out, OPCODE[6], OPCODE[5], not_3_out, not_4_out, OPCODE[2]);
  and and_24 (ALU, OPCODE[6], not_2_out);
  and and_25 (and_25_out, not_1_out, not_2_out, OPCODE[4], not_6_out);
  and and_26 (and_26_out, not_1_out, not_2_out, OPCODE[4], OPCODE[3], OPCODE[2]);
  and and_27 (and_27_out, not_1_out, OPCODE[5], not_3_out, OPCODE[2]);
  and and_28 (and_28_out, not_1_out, OPCODE[5], not_3_out, OPCODE[3]);
  and and_29 (STORE, not_1_out, OPCODE[5], OPCODE[4]);
  and and_30 (and_30_out, not_1_out, not_2_out, not_3_out, not_4_out);
  and and_31 (and_31_out, not_1_out, not_2_out, not_3_out, not_6_out);
  and and_32 (RETURN, OPCODE[6], OPCODE[5], not_3_out, not_4_out);
  and and_33 (JUMP, not_1_out, not_2_out, not_3_out, OPCODE[3], OPCODE[1]);
  and and_34 (GET_PSW, not_1_out, not_2_out, OPCODE[4], not_4_out, OPCODE[1]);
  and and_35 (SET_PSW, not_1_out, not_2_out, OPCODE[4], OPCODE[3], not_5_out, OPCODE[1]);
  and and_36 (GET_LAST_PC, OPCODE[6], OPCODE[5], not_3_out, OPCODE[3]);
  and and_37 (LOAD_HIGH_IMMEDIATE, OPCODE[6], OPCODE[5], OPCODE[4]);
  or or_3 (ALU_OP[2], not_1_out, and_2_out, and_3_out);
  or or_4 (ALU_OP[1], not_1_out, and_4_out, and_5_out, and_6_out);
  or or_5 (ALU_OP[0], and_7_out, and_8_out, and_9_out);
  or or_6 (SHIFTER_OP[1], and_10_out, and_11_out, and_12_out);
  or or_7 (SHIFTER_OP[0], and_13_out, and_14_out, and_15_out);
  or or_8 (BYTE_SIZE[1], not_2_out, and_16_out, and_17_out, OPCODE[6]);
  or or_9 (RELATIVE, and_18_out, and_19_out, and_20_out, and_21_out);
  or or_10 (INTERRUPT, and_22_out, and_23_out);
  or or_11 (SHIFTER, and_25_out, and_26_out);
  or or_12 (LOAD, and_27_out, and_28_out);
  or or_13 (CALL, and_30_out, and_31_out);
endmodule

module Condition_Decoder (
  input  Carry_In,
  input  Negative,
  input  Zero,
  input  Overflow,
  output Never,
  output Always,
  output Not_Equal,
  output Equal,
  output Greater,
  output Less_Or_Equal,
  output Greater_Or_Equal,
  output Less,
  output Is_Positive,
  output Is_Negative,
  output Higher,
  output Lower_Or_Same,
  output Overflow_Clear,
  output Overflow_Set,
  output Carry_Clear,
  output Carry_Set
);

  not not_1 (Carry_Clear, Carry_In);
  not not_2 (Is_Positive, Negative);
  not not_3 (Not_Equal, Zero);
  not not_4 (Overflow_Clear, Overflow);
  xor xor_1 (Less, Overflow, Negative);
  or or_1 (Less_Or_Equal, Zero, Less);
  and and_1 (Lower_Or_Same, Zero, Carry_Clear);
  not not_5 (Greater, Less_Or_Equal);
  not not_6 (Greater_Or_Equal, Less);
  not not_7 (Higher, Lower_Or_Same);

  assign Always = 1'b1;
  assign Carry_Set = Carry_In;
  assign Equal = Zero;
  assign Is_Negative = Negative;
  assign Never = 1'b0;
  assign Overflow_Set = Overflow;
endmodule

module Processor_Status_Word (
  input  Set_Condition_Code,
  input  Write,
  input  Read,
  input  [31:0] LBus_in,
  input  Clock,
  input  Reset,
  input  [3:0] CNZV_in,
  output [31:0] Lbus_out,
  output [9:0] d,
  output [3:0] CNZV_out
);

  wire or_1_out;
  wire [27:6] register_1_q;
  wire [31:0] multiplexer_1_out;

  Multiplexer #(.width(32)) multiplexer_1 (
    .in0(LBus_in), .in1({register_1_q, LBus_in[9:4], CNZV_in}), .out(multiplexer_1_out),
    .sel(Set_Condition_Code));
  or or_1 (or_1_out, Set_Condition_Code, Write);
  Register #(.trigger("falling"), .width(32)) register_1 (
    .D(multiplexer_1_out), .en(or_1_out), .clk(Clock), .Q({register_1_q, d[9:4], CNZV_out}), .clr(Reset));
  assign Lbus_out = Read ? {register_1_q, d[9:4], CNZV_out} : 32'bz;  // Controlled_Buffer controlled_buffer_1

  assign d[3:0] = CNZV_out;
endmodule

module Byte_Decoder (
  input  [1:0] Data_Size,
  input  [1:0] Data_Offset,
  output [2:0] Mux_Enables
);

  wire and_1_out, and_2_out, and_3_out;

  and and_1 (and_1_out, Data_Offset[1], Data_Offset[0]);
  and and_2 (and_2_out, Data_Size[0], Data_Offset[1]);
  and and_3 (and_3_out, Data_Size[0], Data_Offset[0]);
  or or_1 (Mux_Enables[0], Data_Offset[0], Data_Offset[1], Data_Size[0], Data_Size[1]);
  or or_2 (Mux_Enables[2], and_1_out, and_2_out, Data_Size[1]);
  or or_3 (Mux_Enables[1], Data_Offset[1], and_3_out, Data_Size[1]);
endmodule

module IO_Controller (
  input  [1:0] Data_Size,
  input  [31:0] Address_In,
  input  Phase1n,
  input  Phase3s,
  input  Phase3i,
  input  Reset,
  input  Clock,
  input  Read,
  input  Write,
  output Data_2Bytes,
  output Data_4Bytes,
  output [31:0] AddressDebug,
  output [23:0] Address_Out_24Bit,
  output ReadRam,
  output ReadKeyboard,
  output Read_OS_Ram,
  output [7:0] Rom_Address_Out_8Bit,
  output WriteRam,
  output Write_OS_Ram
);

  wire decoder_2_out2, or_1_out;

  Register #(.width(32)) Memory_Address (
    .D(Address_In), .en(or_1_out), .clk(Clock), .Q({AddressDebug[31:24], Address_Out_24Bit}), .clr(Reset));
  or or_1 (or_1_out, Phase1n, Phase3s, Phase3i);
  Decoder #(.select(2)) decoder_1 (
    .out0(WriteRam), .out3(Write_OS_Ram), .sel(AddressDebug[31:30]), .en(Write));  // open: out1, out2
  or or_2 (Data_2Bytes, Data_Size[0], Data_Size[1]);
  Decoder #(.select(2)) decoder_2 (
    .out0(ReadRam), .out1(ReadKeyboard), .out2(decoder_2_out2), .out3(Read_OS_Ram),
    .sel(AddressDebug[31:30]), .en(Read));
  assign Rom_Address_Out_8Bit = decoder_2_out2 ? Address_Out_24Bit[9:2] : 8'bz;  // Controlled_Buffer controlled_buffer_1

  assign AddressDebug[23:0] = Address_Out_24Bit;
  assign Data_4Bytes = Data_Size[1];
endmodule
